// Logisim project DIVISOR.circ as structural Verilog: 3 circuits, main circuit DIVISOR
module SOMADOR (
  input  [7:0] in_1,
  input  [7:0] in_2,
  input  in_3,
  output [7:0] out_4,
  output out_5
);

  wire and_1_out, and_2_out, and_3_out, and_4_out, and_5_out, and_6_out, and_7_out, and_8_out, and_9_out,
       and_10_out, and_11_out, and_12_out, and_13_out, and_14_out, and_15_out, and_16_out, and_17_out,
       and_18_out, and_19_out, and_20_out, and_21_out, and_22_out, and_23_out, and_24_out, and_25_out,
       and_26_out, and_27_out, and_28_out, G0_out, G1_out, G2_out, G3_out, G4_out, G5_out, G6_out, or_1_out,
       or_2_out, or_3_out, or_4_out, or_5_out, or_6_out, or_7_out, P0_out, P1_out, P2_out, P3_out, P4_out,
       P5_out, P6_out;
  wire [7:0] xor_1_out;

  assign xor_1_out = in_2 ^ {8{in_3}};  // XOR_Gate xor_1, 8 bits wide
  A_XOR_B_XOR_C a_xor_b_xor_c_1 (.out_4(out_4[0]), .in_1(xor_1_out[0]), .in_2(in_1[0]), .in_3(in_3));
  A_XOR_B_XOR_C a_xor_b_xor_c_2 (.out_4(out_4[1]), .in_1(in_1[1]), .in_2(xor_1_out[1]), .in_3(or_1_out));
  or P0 (P0_out, in_1[0], xor_1_out[0]);
  and G0 (G0_out, in_1[0], xor_1_out[0]);
  and and_1 (and_1_out, P0_out, in_3);
  or or_1 (or_1_out, G0_out, and_1_out);
  A_XOR_B_XOR_C a_xor_b_xor_c_3 (.out_4(out_4[2]), .in_1(in_1[2]), .in_2(xor_1_out[2]), .in_3(or_2_out));
  and G1 (G1_out, in_1[1], xor_1_out[1]);
  or or_2 (or_2_out, G1_out, and_2_out, and_3_out);
  or P1 (P1_out, in_1[1], xor_1_out[1]);
  and and_2 (and_2_out, P1_out, G0_out);
  and and_3 (and_3_out, P1_out, P0_out, in_3);
  A_XOR_B_XOR_C a_xor_b_xor_c_4 (.out_4(out_4[3]), .in_1(in_1[3]), .in_2(xor_1_out[3]), .in_3(or_3_out));
  or P2 (P2_out, in_1[2], xor_1_out[2]);
  and G2 (G2_out, in_1[2], xor_1_out[2]);
  and and_4 (and_4_out, P2_out, G1_out);
  or or_3 (or_3_out, G2_out, and_4_out, and_5_out, and_6_out);
  and and_5 (and_5_out, G0_out, P1_out, P2_out);
  and and_6 (and_6_out, in_3, P0_out, P1_out, P2_out);
  A_XOR_B_XOR_C a_xor_b_xor_c_5 (.out_4(out_4[4]), .in_1(in_1[4]), .in_2(xor_1_out[4]), .in_3(or_4_out));
  and G3 (G3_out, in_1[3], xor_1_out[3]);
  or or_4 (or_4_out, G3_out, and_7_out, and_8_out, and_9_out, and_10_out);
  or P3 (P3_out, in_1[3], xor_1_out[3]);
  and and_7 (and_7_out, P3_out, G2_out);
  and and_8 (and_8_out, G1_out, P2_out, P3_out);
  and and_9 (and_9_out, G0_out, P1_out, P2_out, P3_out);
  and and_10 (and_10_out, in_3, P0_out, P1_out, P2_out, P3_out);
  and G4 (G4_out, in_1[4], xor_1_out[4]);
  A_XOR_B_XOR_C a_xor_b_xor_c_6 (.out_4(out_4[5]), .in_1(in_1[5]), .in_2(xor_1_out[5]), .in_3(or_5_out));
  or P4 (P4_out, in_1[4], xor_1_out[4]);
  and and_11 (and_11_out, P4_out, G3_out);
  and and_12 (and_12_out, G2_out, P3_out, P4_out);
  or or_5 (or_5_out, G4_out, and_11_out, and_12_out, and_13_out, and_14_out, and_15_out);
  and and_13 (and_13_out, G1_out, P2_out, P3_out, P4_out);
  and and_14 (and_14_out, G0_out, P1_out, P2_out, P3_out, P4_out);
  and and_15 (and_15_out, in_3, P0_out, P1_out, P2_out, P3_out, P4_out);
  A_XOR_B_XOR_C a_xor_b_xor_c_7 (.out_4(out_4[6]), .in_1(in_1[6]), .in_2(xor_1_out[6]), .in_3(or_6_out));
  or P5 (P5_out, in_1[5], xor_1_out[5]);
  and G5 (G5_out, in_1[5], xor_1_out[5]);
  and and_16 (and_16_out, P5_out, G4_out);
  or or_6 (or_6_out, G5_out, and_16_out, and_17_out, and_19_out, and_18_out, and_20_out, and_21_out);
  and and_17 (and_17_out, G3_out, P4_out, P5_out);
  and and_18 (and_18_out, G1_out, P2_out, P3_out, P4_out, P5_out);
  and and_19 (and_19_out, G2_out, P3_out, P4_out, P5_out);
  and and_20 (and_20_out, G0_out, P1_out, P2_out, P3_out, P4_out, P5_out);
  and and_21 (and_21_out, in_3, P0_out, P1_out, P2_out, P3_out, P4_out, P5_out);
  A_XOR_B_XOR_C a_xor_b_xor_c_8 (.out_4(out_4[7]), .in_1(in_1[7]), .in_2(xor_1_out[7]), .in_3(or_7_out));
  or P6 (P6_out, in_1[6], xor_1_out[6]);
  and G6 (G6_out, in_1[6], xor_1_out[6]);
  and and_22 (and_22_out, P6_out, G5_out);
  or or_7 (or_7_out, G6_out, and_22_out, and_23_out, and_24_out, and_25_out, and_26_out, and_27_out, and_28_out);
  and and_23 (and_23_out, G4_out, P5_out, P6_out);
  and and_24 (and_24_out, G3_out, P4_out, P5_out, P6_out);
  and and_25 (and_25_out, G2_out, P3_out, P4_out, P5_out, P6_out);
  and and_26 (and_26_out, G1_out, P2_out, P3_out, P4_out, P5_out, P6_out);
  and and_27 (and_27_out, G0_out, P1_out, P2_out, P3_out, P4_out, P5_out, P6_out);
  and and_28 (and_28_out, in_3, P0_out, P1_out, P2_out, P3_out, P4_out, P5_out, P6_out);

  assign out_5 = out_4[7];
endmodule

module A_XOR_B_XOR_C (
  input  in_1,
  input  in_2,
  input  in_3,
  output out_4
);

  wire xor_1_out;

  xor xor_1 (xor_1_out, in_3, in_2);
  xor xor_2 (out_4, xor_1_out, in_1);
endmodule

module DIVISOR (
  input  [7:0] in_1,
  input  [7:0] in_2,
  output [7:0] out_3,
  output [7:0] out_4
);

  wire somador_1_out_5, somador_2_out_5, somador_3_out_5, somador_4_out_5, somador_5_out_5, somador_6_out_5,
       somador_7_out_5, somador_8_out_5;
  wire [7:0] multiplexer_1_out, multiplexer_2_out, multiplexer_3_out, multiplexer_4_out, multiplexer_5_out,
       multiplexer_7_out, somador_1_out_4, somador_2_out_4, somador_3_out_4, somador_4_out_4,
       somador_5_out_4, somador_6_out_4, somador_7_out_4, somador_8_out_4;
  wire [7:1] multiplexer_6_out_2;
  wire [7:7] multiplexer_6_out;

  SOMADOR somador_1 (
    .in_1({{7{1'b0}}, in_1[7]}), .in_2(in_2), .in_3(1'b1), .out_4(somador_1_out_4), .out_5(somador_1_out_5));
  Multiplexer #(.width(8), .enable("false")) multiplexer_1 (
    .in0(somador_1_out_4), .in1({{7{1'b0}}, in_1[7]}), .out(multiplexer_1_out), .sel(somador_1_out_5));
  SOMADOR somador_2 (
    .in_1({multiplexer_1_out[6:0], in_1[6]}), .in_2(in_2), .in_3(1'b1), .out_4(somador_2_out_4),
    .out_5(somador_2_out_5));
  Multiplexer #(.width(8), .enable("false")) multiplexer_2 (
    .in0(somador_2_out_4), .in1({multiplexer_1_out[6:0], in_1[6]}), .out(multiplexer_2_out),
    .sel(somador_2_out_5));
  not not_1 (out_4[5], somador_3_out_5);
  not not_2 (out_4[7], somador_1_out_5);
  not not_3 (out_4[6], somador_2_out_5);
  not not_4 (out_4[1], somador_7_out_5);
  not not_5 (out_4[3], somador_5_out_5);
  not not_6 (out_4[2], somador_6_out_5);
  not not_7 (out_4[0], somador_8_out_5);
  not not_8 (out_4[4], somador_4_out_5);
  SOMADOR somador_3 (
    .in_1({multiplexer_2_out[6:0], in_1[5]}), .in_2(in_2), .in_3(1'b1), .out_4(somador_3_out_4),
    .out_5(somador_3_out_5));
  Multiplexer #(.width(8), .enable("false")) multiplexer_3 (
    .in0(somador_3_out_4), .in1({multiplexer_2_out[6:0], in_1[5]}), .out(multiplexer_3_out),
    .sel(somador_3_out_5));
  SOMADOR somador_4 (
    .in_1({multiplexer_3_out[6:0], in_1[4]}), .in_2(in_2), .in_3(1'b1), .out_4(somador_4_out_4),
    .out_5(somador_4_out_5));
  Multiplexer #(.width(8), .enable("false")) multiplexer_4 (
    .in0(somador_4_out_4), .in1({multiplexer_3_out[6:0], in_1[4]}), .out(multiplexer_4_out),
    .sel(somador_4_out_5));
  SOMADOR somador_5 (
    .in_1({multiplexer_4_out[6:0], in_1[3]}), .in_2(in_2), .in_3(1'b1), .out_4(somador_5_out_4),
    .out_5(somador_5_out_5));
  Multiplexer #(.width(8), .enable("false")) multiplexer_5 (
    .in0(somador_5_out_4), .in1({multiplexer_4_out[6:0], in_1[3]}), .out(multiplexer_5_out),
    .sel(somador_5_out_5));
  SOMADOR somador_6 (
    .in_1({multiplexer_5_out[6:0], in_1[2]}), .in_2(in_2), .in_3(1'b1), .out_4(somador_6_out_4),
    .out_5(somador_6_out_5));
  Multiplexer #(.width(8), .enable("false")) multiplexer_6 (
    .in0(somador_6_out_4), .in1({multiplexer_5_out[6:0], in_1[2]}),
    .out({multiplexer_6_out[7], multiplexer_6_out_2}), .sel(somador_6_out_5));
  SOMADOR somador_7 (
    .in_1({multiplexer_6_out_2, in_1[1]}), .in_2(in_2), .in_3(1'b1), .out_4(somador_7_out_4),
    .out_5(somador_7_out_5));
  Multiplexer #(.width(8), .enable("false")) multiplexer_7 (
    .in0(somador_7_out_4), .in1({multiplexer_6_out_2, in_1[1]}), .out(multiplexer_7_out),
    .sel(somador_7_out_5));
  SOMADOR somador_8 (
    .in_1({multiplexer_7_out[6:0], in_1[0]}), .in_2(in_2), .in_3(1'b1), .out_4(somador_8_out_4),
    .out_5(somador_8_out_5));
  Multiplexer #(.width(8), .enable("false")) multiplexer_8 (
    .in0(somador_8_out_4), .in1({multiplexer_7_out[6:0], in_1[0]}), .out(out_3), .sel(somador_8_out_5));

  // Other names for the same wires on the sheet: Dividendo[7:0] = in_1; Divisor[7:0] = in_2; Resto[7:0] = out_3;
  //   Resultado[7:0] = out_4
endmodule
