// Logisim project LogisimCalculadoraMultiplicacao1.circ as structural Verilog: 5 circuits, main circuit main
// s1
module main (
  input  A,
  input  B,
  input  C,
  output S
);

  wire xor_1_out;

  xor xor_1 (xor_1_out, C, B);
  xor xor_2 (S, xor_1_out, A);
endmodule

module exc1 (
  input  [7:0] A,
  input  [7:0] B,
  input  in_3,
  output [7:0] c
);

  wire and_1_out, and_2_out, and_3_out, and_4_out, and_5_out, and_6_out, G0_out, G1_out, G2_out, or_1_out,
       or_2_out, or_3_out, P0_out, P1_out, P2_out;
  wire [7:0] xor_1_out;

  assign xor_1_out = B ^ {8{in_3}};  // XOR_Gate xor_1, 8 bits wide
  main main_1 (.S(c[0]), .A(A[0]), .B(xor_1_out[0]), .C(in_3));
  and G0 (G0_out, A[0], xor_1_out[0]);
  main main_2 (.S(c[1]), .A(A[1]), .B(xor_1_out[1]), .C(or_1_out));
  or P0 (P0_out, A[0], xor_1_out[0]);
  and and_1 (and_1_out, P0_out, in_3);
  or or_1 (or_1_out, G0_out, and_1_out);
  and G1 (G1_out, A[1], xor_1_out[1]);
  main main_3 (.S(c[2]), .A(A[2]), .B(xor_1_out[2]), .C(or_2_out));
  or P1 (P1_out, A[1], xor_1_out[1]);
  and and_2 (and_2_out, G0_out, P1_out);
  and and_3 (and_3_out, P1_out, P0_out, in_3);
  or or_2 (or_2_out, G1_out, and_2_out, and_3_out);
  and G2 (G2_out, A[2], xor_1_out[3]);
  main main_4 (.S(c[3]), .A(A[3]), .B(xor_1_out[3]), .C(or_3_out));
  or P2 (P2_out, A[2], xor_1_out[3]);
  and and_4 (and_4_out, P0_out, P2_out);
  and and_5 (and_5_out, in_3, G0_out, P0_out);
  or or_3 (or_3_out, G2_out, and_4_out, and_5_out, and_6_out);
  and and_6 (and_6_out, in_3, G0_out, P1_out, P0_out);
endmodule

module aula_20_04 (
  input  [7:0] in_1,
  input  [7:0] in_2,
  output [7:0] out_3
);

  wire and_1_out, and_2_out, and_3_out, and_4_out, and_5_out, and_6_out, and_7_out, and_8_out, and_9_out,
       and_10_out, and_11_out, and_12_out, and_13_out, and_14_out, and_15_out, and_16_out, and_17_out,
       and_18_out, and_19_out, and_20_out, and_21_out, and_22_out, and_23_out, and_24_out, and_25_out,
       and_26_out, and_27_out, and_28_out, and_29_out, and_30_out, and_31_out, and_32_out, and_33_out,
       and_34_out, and_35_out, and_36_out, and_37_out, and_38_out, and_39_out, and_40_out, and_41_out,
       and_42_out, and_43_out, and_44_out, and_45_out, and_46_out, and_47_out, and_48_out, and_49_out,
       and_50_out, and_51_out, and_52_out, and_53_out, and_54_out, and_55_out, and_56_out, and_57_out,
       and_58_out, and_59_out, and_60_out, and_61_out, and_62_out, and_63_out, fulladder_1_cout,
       fulladder_1_s, fulladder_2_cout, fulladder_4_cout, fulladder_4_s, fulladder_5_cout, fulladder_5_s,
       fulladder_6_cout, fulladder_7_cout, fulladder_8_cout, fulladder_8_s, fulladder_9_cout, fulladder_9_s,
       fulladder_10_cout, fulladder_10_s, fulladder_11_cout, fulladder_11_s, fulladder_12_cout,
       fulladder_12_s, fulladder_13_cout, fulladder_13_s, fulladder_14_cout, fulladder_14_s,
       fulladder_15_cout, fulladder_16_cout, fulladder_16_s, fulladder_17_cout, fulladder_17_s,
       fulladder_18_cout, fulladder_18_s, fulladder_19_cout, fulladder_19_s, fulladder_20_cout,
       fulladder_20_s, fulladder_21_cout, fulladder_21_s, fulladder_22_cout, fulladder_22_s,
       fulladder_23_cout, fulladder_23_s, fulladder_24_cout, fulladder_24_s, fulladder_25_cout,
       fulladder_25_s, fulladder_26_cout, fulladder_27_cout, fulladder_28_cout, fulladder_28_s,
       fulladder_29_cout, fulladder_29_s, fulladder_30_cout, fulladder_30_s, fulladder_31_cout,
       fulladder_31_s, fulladder_32_cout, fulladder_32_s, fulladder_33_cout, fulladder_33_s,
       fulladder_34_cout, fulladder_34_s, fulladder_35_cout, fulladder_35_s, fulladder_36_cout,
       fulladder_36_s, fulladder_37_cout, fulladder_37_s, fulladder_38_cout, fulladder_38_s,
       fulladder_39_cout, fulladder_39_s, fulladder_40_cout, fulladder_40_s, fulladder_41_cout,
       fulladder_41_s, fulladder_42_cout, fulladder_42_s, fulladder_43_cout, fulladder_43_s,
       fulladder_44_cout, fulladder_44_s, fulladder_45_cout, fulladder_45_s, fulladder_46_cout,
       fulladder_46_s, fulladder_47_cout, fulladder_47_s, fulladder_48_cout, fulladder_48_s,
       halfadder_1_cout, halfadder_1_s, halfadder_2_cout, halfadder_3_cout, halfadder_4_cout,
       halfadder_5_cout, halfadder_6_cout, halfadder_7_cout, halfadder_8_cout;
  wire [15:8] fulladder_26_s;

  and and_1 (and_1_out, in_1[7], in_2[7]);
  and and_2 (and_2_out, in_1[7], in_2[6]);
  fullAdder fulladder_1 (
    .A(and_2_out), .B(fulladder_4_cout), .C(fulladder_5_cout), .S(fulladder_1_s), .Cout(fulladder_1_cout));
  and and_3 (and_3_out, in_1[6], in_2[7]);
  fullAdder fulladder_2 (
    .A(and_3_out), .B(fulladder_1_s), .C(fulladder_6_cout), .S(fulladder_26_s[13]), .Cout(fulladder_2_cout));
  fullAdder fulladder_3 (
    .A(and_1_out), .B(fulladder_1_cout), .C(fulladder_2_cout), .S(fulladder_26_s[14]),
    .Cout(fulladder_26_s[15]));
  and and_4 (and_4_out, in_1[7], in_2[4]);
  and and_5 (and_5_out, in_1[6], in_2[5]);
  and and_6 (and_6_out, in_1[7], in_2[5]);
  fullAdder fulladder_4 (
    .A(and_6_out), .B(fulladder_9_cout), .C(fulladder_12_cout), .S(fulladder_4_s), .Cout(fulladder_4_cout));
  and and_7 (and_7_out, in_1[6], in_2[6]);
  and and_8 (and_8_out, in_1[5], in_2[6]);
  fullAdder fulladder_5 (
    .A(and_7_out), .B(fulladder_4_s), .C(fulladder_13_cout), .S(fulladder_5_s), .Cout(fulladder_5_cout));
  and and_9 (and_9_out, in_1[5], in_2[7]);
  and and_10 (and_10_out, in_1[4], in_2[7]);
  fullAdder fulladder_6 (
    .A(and_9_out), .B(fulladder_5_s), .C(fulladder_7_cout), .S(fulladder_26_s[12]), .Cout(fulladder_6_cout));
  fullAdder fulladder_7 (
    .A(and_10_out), .B(fulladder_13_s), .C(fulladder_15_cout), .S(fulladder_26_s[11]), .Cout(fulladder_7_cout));
  and and_11 (and_11_out, in_1[7], in_2[2]);
  and and_12 (and_12_out, in_1[7], in_2[3]);
  and and_13 (and_13_out, in_1[6], in_2[3]);
  fullAdder fulladder_8 (
    .A(and_12_out), .B(fulladder_17_cout), .C(fulladder_19_cout), .S(fulladder_8_s), .Cout(fulladder_8_cout));
  and and_14 (and_14_out, in_1[6], in_2[4]);
  fullAdder fulladder_9 (
    .A(and_4_out), .B(fulladder_8_cout), .C(fulladder_10_cout), .S(fulladder_9_s), .Cout(fulladder_9_cout));
  fullAdder fulladder_10 (
    .A(and_14_out), .B(fulladder_8_s), .C(fulladder_20_cout), .S(fulladder_10_s), .Cout(fulladder_10_cout));
  and and_15 (and_15_out, in_1[5], in_2[5]);
  fullAdder fulladder_11 (
    .A(and_15_out), .B(fulladder_10_s), .C(fulladder_22_cout), .S(fulladder_11_s), .Cout(fulladder_11_cout));
  fullAdder fulladder_12 (
    .A(and_5_out), .B(fulladder_9_s), .C(fulladder_11_cout), .S(fulladder_12_s), .Cout(fulladder_12_cout));
  and and_16 (and_16_out, in_1[4], in_2[6]);
  fullAdder fulladder_13 (
    .A(and_8_out), .B(fulladder_12_s), .C(fulladder_14_cout), .S(fulladder_13_s), .Cout(fulladder_13_cout));
  fullAdder fulladder_14 (
    .A(and_16_out), .B(fulladder_11_s), .C(fulladder_24_cout), .S(fulladder_14_s), .Cout(fulladder_14_cout));
  and and_17 (and_17_out, in_1[2], in_2[7]);
  and and_18 (and_18_out, in_1[3], in_2[7]);
  fullAdder fulladder_15 (
    .A(and_18_out), .B(fulladder_14_s), .C(fulladder_27_cout), .S(fulladder_26_s[10]),
    .Cout(fulladder_15_cout));
  and and_19 (and_19_out, in_1[7], in_2[1]);
  halfAdder halfadder_1 (.A(and_19_out), .B(fulladder_28_cout), .S(halfadder_1_s), .Cout(halfadder_1_cout));
  and and_20 (and_20_out, in_1[6], in_2[2]);
  fullAdder fulladder_16 (
    .A(and_20_out), .B(halfadder_1_s), .C(fulladder_29_cout), .S(fulladder_16_s), .Cout(fulladder_16_cout));
  fullAdder fulladder_17 (
    .A(and_11_out), .B(halfadder_1_cout), .C(fulladder_16_cout), .S(fulladder_17_s), .Cout(fulladder_17_cout));
  and and_21 (and_21_out, in_1[5], in_2[3]);
  fullAdder fulladder_18 (
    .A(and_21_out), .B(fulladder_16_s), .C(fulladder_30_cout), .S(fulladder_18_s), .Cout(fulladder_18_cout));
  fullAdder fulladder_19 (
    .A(and_13_out), .B(fulladder_17_s), .C(fulladder_18_cout), .S(fulladder_19_s), .Cout(fulladder_19_cout));
  and and_22 (and_22_out, in_1[4], in_2[4]);
  and and_23 (and_23_out, in_1[5], in_2[4]);
  fullAdder fulladder_20 (
    .A(and_23_out), .B(fulladder_19_s), .C(fulladder_21_cout), .S(fulladder_20_s), .Cout(fulladder_20_cout));
  fullAdder fulladder_21 (
    .A(and_22_out), .B(fulladder_18_s), .C(fulladder_31_cout), .S(fulladder_21_s), .Cout(fulladder_21_cout));
  and and_24 (and_24_out, in_1[4], in_2[5]);
  and and_25 (and_25_out, in_1[3], in_2[5]);
  fullAdder fulladder_22 (
    .A(and_24_out), .B(fulladder_20_s), .C(fulladder_23_cout), .S(fulladder_22_s), .Cout(fulladder_22_cout));
  fullAdder fulladder_23 (
    .A(and_25_out), .B(fulladder_21_s), .C(fulladder_32_cout), .S(fulladder_23_s), .Cout(fulladder_23_cout));
  and and_26 (and_26_out, in_1[3], in_2[6]);
  and and_27 (and_27_out, in_1[2], in_2[6]);
  fullAdder fulladder_24 (
    .A(and_26_out), .B(fulladder_22_s), .C(fulladder_25_cout), .S(fulladder_24_s), .Cout(fulladder_24_cout));
  fullAdder fulladder_25 (
    .A(and_27_out), .B(fulladder_23_s), .C(fulladder_33_cout), .S(fulladder_25_s), .Cout(fulladder_25_cout));
  and and_28 (and_28_out, in_1[1], in_2[7]);
  fullAdder fulladder_26 (
    .A(and_28_out), .B(fulladder_25_s), .C(halfadder_2_cout), .S(fulladder_26_s[8]), .Cout(fulladder_26_cout));
  fullAdder fulladder_27 (
    .A(and_17_out), .B(fulladder_24_s), .C(fulladder_26_cout), .S(fulladder_26_s[9]), .Cout(fulladder_27_cout));
  and and_29 (and_29_out, in_1[6], in_2[0]);
  and and_30 (and_30_out, in_1[7], in_2[0]);
  and and_31 (and_31_out, in_1[5], in_2[1]);
  and and_32 (and_32_out, in_1[6], in_2[1]);
  fullAdder fulladder_28 (
    .A(and_32_out), .B(and_30_out), .C(fulladder_34_cout), .S(fulladder_28_s), .Cout(fulladder_28_cout));
  and and_33 (and_33_out, in_1[4], in_2[2]);
  and and_34 (and_34_out, in_1[5], in_2[2]);
  fullAdder fulladder_29 (
    .A(and_34_out), .B(fulladder_28_s), .C(fulladder_36_cout), .S(fulladder_29_s), .Cout(fulladder_29_cout));
  and and_35 (and_35_out, in_1[3], in_2[3]);
  and and_36 (and_36_out, in_1[4], in_2[3]);
  fullAdder fulladder_30 (
    .A(and_36_out), .B(fulladder_29_s), .C(fulladder_39_cout), .S(fulladder_30_s), .Cout(fulladder_30_cout));
  and and_37 (and_37_out, in_1[2], in_2[4]);
  and and_38 (and_38_out, in_1[3], in_2[4]);
  fullAdder fulladder_31 (
    .A(and_38_out), .B(fulladder_30_s), .C(fulladder_41_cout), .S(fulladder_31_s), .Cout(fulladder_31_cout));
  and and_39 (and_39_out, in_1[1], in_2[5]);
  and and_40 (and_40_out, in_1[2], in_2[5]);
  fullAdder fulladder_32 (
    .A(and_40_out), .B(fulladder_31_s), .C(fulladder_42_cout), .S(fulladder_32_s), .Cout(fulladder_32_cout));
  and and_41 (and_41_out, in_1[0], in_2[6]);
  and and_42 (and_42_out, in_1[1], in_2[6]);
  fullAdder fulladder_33 (
    .A(and_42_out), .B(fulladder_32_s), .C(halfadder_4_cout), .S(fulladder_33_s), .Cout(fulladder_33_cout));
  and and_43 (and_43_out, in_1[0], in_2[7]);
  halfAdder halfadder_2 (.A(and_43_out), .B(fulladder_33_s), .S(out_3[7]), .Cout(halfadder_2_cout));
  and and_44 (and_44_out, in_1[5], in_2[0]);
  and and_45 (and_45_out, in_1[4], in_2[1]);
  fullAdder fulladder_34 (
    .A(and_31_out), .B(and_29_out), .C(fulladder_35_cout), .S(fulladder_34_s), .Cout(fulladder_34_cout));
  fullAdder fulladder_35 (
    .A(and_45_out), .B(and_44_out), .C(fulladder_44_cout), .S(fulladder_35_s), .Cout(fulladder_35_cout));
  and and_46 (and_46_out, in_1[3], in_2[2]);
  fullAdder fulladder_36 (
    .A(and_33_out), .B(fulladder_34_s), .C(fulladder_37_cout), .S(fulladder_36_s), .Cout(fulladder_36_cout));
  fullAdder fulladder_37 (
    .A(and_46_out), .B(fulladder_35_s), .C(fulladder_46_cout), .S(fulladder_37_s), .Cout(fulladder_37_cout));
  and and_47 (and_47_out, in_1[2], in_2[3]);
  fullAdder fulladder_38 (
    .A(and_47_out), .B(fulladder_37_s), .C(fulladder_47_cout), .S(fulladder_38_s), .Cout(fulladder_38_cout));
  fullAdder fulladder_39 (
    .A(and_35_out), .B(fulladder_36_s), .C(fulladder_38_cout), .S(fulladder_39_s), .Cout(fulladder_39_cout));
  and and_48 (and_48_out, in_1[1], in_2[4]);
  fullAdder fulladder_40 (
    .A(and_48_out), .B(fulladder_38_s), .C(halfadder_6_cout), .S(fulladder_40_s), .Cout(fulladder_40_cout));
  fullAdder fulladder_41 (
    .A(and_37_out), .B(fulladder_39_s), .C(fulladder_40_cout), .S(fulladder_41_s), .Cout(fulladder_41_cout));
  and and_49 (and_49_out, in_1[0], in_2[5]);
  fullAdder fulladder_42 (
    .A(and_39_out), .B(fulladder_41_s), .C(halfadder_3_cout), .S(fulladder_42_s), .Cout(fulladder_42_cout));
  halfAdder halfadder_3 (.A(and_49_out), .B(fulladder_40_s), .S(out_3[5]), .Cout(halfadder_3_cout));
  halfAdder halfadder_4 (.A(and_41_out), .B(fulladder_42_s), .S(out_3[6]), .Cout(halfadder_4_cout));
  and and_50 (and_50_out, in_1[4], in_2[0]);
  and and_51 (and_51_out, in_1[3], in_2[0]);
  and and_52 (and_52_out, in_1[3], in_2[1]);
  and and_53 (and_53_out, in_1[2], in_2[1]);
  fullAdder fulladder_43 (
    .A(and_53_out), .B(and_51_out), .C(fulladder_48_cout), .S(fulladder_43_s), .Cout(fulladder_43_cout));
  fullAdder fulladder_44 (
    .A(and_52_out), .B(and_50_out), .C(fulladder_43_cout), .S(fulladder_44_s), .Cout(fulladder_44_cout));
  and and_54 (and_54_out, in_1[2], in_2[2]);
  and and_55 (and_55_out, in_1[1], in_2[2]);
  fullAdder fulladder_45 (
    .A(and_55_out), .B(fulladder_43_s), .C(halfadder_7_cout), .S(fulladder_45_s), .Cout(fulladder_45_cout));
  fullAdder fulladder_46 (
    .A(and_54_out), .B(fulladder_44_s), .C(fulladder_45_cout), .S(fulladder_46_s), .Cout(fulladder_46_cout));
  and and_56 (and_56_out, in_1[1], in_2[3]);
  and and_57 (and_57_out, in_1[0], in_2[3]);
  halfAdder halfadder_5 (.A(and_57_out), .B(fulladder_45_s), .S(out_3[3]), .Cout(halfadder_5_cout));
  fullAdder fulladder_47 (
    .A(and_56_out), .B(fulladder_46_s), .C(halfadder_5_cout), .S(fulladder_47_s), .Cout(fulladder_47_cout));
  and and_58 (and_58_out, in_1[0], in_2[4]);
  halfAdder halfadder_6 (.A(and_58_out), .B(fulladder_47_s), .S(out_3[4]), .Cout(halfadder_6_cout));
  and and_59 (and_59_out, in_1[2], in_2[0]);
  and and_60 (and_60_out, in_1[1], in_2[0]);
  and and_61 (and_61_out, in_1[1], in_2[1]);
  and and_62 (and_62_out, in_1[0], in_2[1]);
  fullAdder fulladder_48 (
    .A(and_61_out), .B(and_59_out), .C(halfadder_8_cout), .S(fulladder_48_s), .Cout(fulladder_48_cout));
  and and_63 (and_63_out, in_1[0], in_2[2]);
  halfAdder halfadder_7 (.A(and_63_out), .B(fulladder_48_s), .S(out_3[2]), .Cout(halfadder_7_cout));
  and and_64 (out_3[0], in_1[0], in_2[0]);
  halfAdder halfadder_8 (.A(and_62_out), .B(and_60_out), .S(out_3[1]), .Cout(halfadder_8_cout));

  // Other names for the same wires on the sheet: A0 = in_1[0]; A1 = in_1[1]; A2 = in_1[2]; A3 = in_1[3]; A4 = in_1[4];
  //   A5 = in_1[5]; A6 = in_1[6]; A7 = in_1[7]; B0 = in_2[0]; B1 = in_2[1]; B2 = in_2[2]; B3 = in_2[3]; B4 = in_2[4];
  //   B5 = in_2[5]; B6 = in_2[6]; B7 = in_2[7]
endmodule

module fullAdder (
  input  A,
  input  B,
  input  C,
  output S,
  output Cout
);

  wire and_1_out, and_2_out, and_3_out, and_4_out, and_5_out, and_6_out, and_7_out, not_1_out, not_2_out,
       not_3_out, not_4_out, not_5_out, not_6_out;

  not not_1 (not_1_out, A);
  not not_2 (not_2_out, B);
  not not_3 (not_3_out, A);
  not not_4 (not_4_out, C);
  not not_5 (not_5_out, B);
  not not_6 (not_6_out, C);
  and and_1 (and_1_out, B, C);
  and and_2 (and_2_out, A, C);
  and and_3 (and_3_out, A, B);
  and and_4 (and_4_out, not_1_out, not_2_out, C);
  and and_5 (and_5_out, not_3_out, B, not_4_out);
  and and_6 (and_6_out, A, not_5_out, not_6_out);
  and and_7 (and_7_out, A, B, C);
  or or_1 (Cout, and_1_out, and_2_out, and_3_out);
  or or_2 (S, and_4_out, and_5_out, and_6_out, and_7_out);
endmodule

module halfAdder (
  input  A,
  input  B,
  output S,
  output Cout
);

  wire and_2_out, and_3_out, not_1_out, not_2_out;

  not not_1 (not_1_out, A);
  not not_2 (not_2_out, B);
  and and_1 (Cout, A, B);
  and and_2 (and_2_out, not_1_out, B);
  and and_3 (and_3_out, A, not_2_out);
  or or_1 (S, and_2_out, and_3_out);
endmodule
