// Logisim project MULTIPLCIADOR.circ as structural Verilog: 4 circuits, main circuit A XOR B XOR C
// s1
module A_XOR_B_XOR_C (
  input  A,
  input  B,
  input  C,
  output S
);

  wire xor_1_out;

  xor xor_1 (xor_1_out, C, B);
  xor xor_2 (S, xor_1_out, A);
endmodule

module MULTIPLICADOR_9_BITS (
  input  [7:0] in_1,
  input  [7:0] in_2,
  output [7:0] out_3
);

  wire and_1_out, and_2_out, and_3_out, and_4_out, and_5_out, and_6_out, and_7_out, and_8_out, and_9_out,
       and_10_out, and_11_out, and_12_out, and_13_out, and_14_out, and_15_out, and_16_out, and_17_out,
       and_18_out, and_19_out, and_20_out, and_21_out, and_22_out, and_23_out, and_24_out, and_25_out,
       and_26_out, and_27_out, and_28_out, and_29_out, and_30_out, and_31_out, and_32_out, and_33_out,
       and_34_out, and_35_out, and_36_out, and_37_out, and_38_out, and_39_out, and_40_out, and_41_out,
       and_42_out, and_43_out, and_44_out, and_45_out, and_46_out, and_47_out, and_48_out, and_49_out,
       and_50_out, and_51_out, and_52_out, and_53_out, and_54_out, and_55_out, and_56_out, and_57_out,
       and_58_out, and_59_out, and_60_out, and_61_out, and_62_out, and_63_out, full_adder_1_cout,
       full_adder_1_s, full_adder_2_cout, full_adder_4_cout, full_adder_4_s, full_adder_5_cout,
       full_adder_5_s, full_adder_6_cout, full_adder_7_cout, full_adder_8_cout, full_adder_8_s,
       full_adder_9_cout, full_adder_9_s, full_adder_10_cout, full_adder_10_s, full_adder_11_cout,
       full_adder_11_s, full_adder_12_cout, full_adder_12_s, full_adder_13_cout, full_adder_13_s,
       full_adder_14_cout, full_adder_14_s, full_adder_15_cout, full_adder_16_cout, full_adder_16_s,
       full_adder_17_cout, full_adder_17_s, full_adder_18_cout, full_adder_18_s, full_adder_19_cout,
       full_adder_19_s, full_adder_20_cout, full_adder_20_s, full_adder_21_cout, full_adder_21_s,
       full_adder_22_cout, full_adder_22_s, full_adder_23_cout, full_adder_23_s, full_adder_24_cout,
       full_adder_24_s, full_adder_25_cout, full_adder_25_s, full_adder_26_cout, full_adder_27_cout,
       full_adder_28_cout, full_adder_28_s, full_adder_29_cout, full_adder_29_s, full_adder_30_cout,
       full_adder_30_s, full_adder_31_cout, full_adder_31_s, full_adder_32_cout, full_adder_32_s,
       full_adder_33_cout, full_adder_33_s, full_adder_34_cout, full_adder_34_s, full_adder_35_cout,
       full_adder_35_s, full_adder_36_cout, full_adder_36_s, full_adder_37_cout, full_adder_37_s,
       full_adder_38_cout, full_adder_38_s, full_adder_39_cout, full_adder_39_s, full_adder_40_cout,
       full_adder_40_s, full_adder_41_cout, full_adder_41_s, full_adder_42_cout, full_adder_42_s,
       full_adder_43_cout, full_adder_43_s, full_adder_44_cout, full_adder_44_s, full_adder_45_cout,
       full_adder_45_s, full_adder_46_cout, full_adder_46_s, full_adder_47_cout, full_adder_47_s,
       full_adder_48_cout, full_adder_48_s, half_adder_1_cout, half_adder_1_s, half_adder_2_cout,
       half_adder_3_cout, half_adder_4_cout, half_adder_5_cout, half_adder_6_cout, half_adder_7_cout,
       half_adder_8_cout;
  wire [15:8] full_adder_26_s;

  and and_1 (and_1_out, in_1[7], in_2[7]);
  and and_2 (and_2_out, in_1[7], in_2[6]);
  FULL_ADDER full_adder_1 (
    .A(and_2_out), .B(full_adder_4_cout), .C(full_adder_5_cout), .S(full_adder_1_s), .Cout(full_adder_1_cout));
  and and_3 (and_3_out, in_1[6], in_2[7]);
  FULL_ADDER full_adder_2 (
    .A(and_3_out), .B(full_adder_1_s), .C(full_adder_6_cout), .S(full_adder_26_s[13]),
    .Cout(full_adder_2_cout));
  FULL_ADDER full_adder_3 (
    .A(and_1_out), .B(full_adder_1_cout), .C(full_adder_2_cout), .S(full_adder_26_s[14]),
    .Cout(full_adder_26_s[15]));
  and and_4 (and_4_out, in_1[7], in_2[4]);
  and and_5 (and_5_out, in_1[6], in_2[5]);
  and and_6 (and_6_out, in_1[7], in_2[5]);
  FULL_ADDER full_adder_4 (
    .A(and_6_out), .B(full_adder_9_cout), .C(full_adder_12_cout), .S(full_adder_4_s), .Cout(full_adder_4_cout));
  and and_7 (and_7_out, in_1[6], in_2[6]);
  and and_8 (and_8_out, in_1[5], in_2[6]);
  FULL_ADDER full_adder_5 (
    .A(and_7_out), .B(full_adder_4_s), .C(full_adder_13_cout), .S(full_adder_5_s), .Cout(full_adder_5_cout));
  and and_9 (and_9_out, in_1[4], in_2[7]);
  and and_10 (and_10_out, in_1[5], in_2[7]);
  FULL_ADDER full_adder_6 (
    .A(and_10_out), .B(full_adder_5_s), .C(full_adder_7_cout), .S(full_adder_26_s[12]),
    .Cout(full_adder_6_cout));
  FULL_ADDER full_adder_7 (
    .A(and_9_out), .B(full_adder_13_s), .C(full_adder_15_cout), .S(full_adder_26_s[11]),
    .Cout(full_adder_7_cout));
  and and_11 (and_11_out, in_1[7], in_2[2]);
  and and_12 (and_12_out, in_1[7], in_2[3]);
  and and_13 (and_13_out, in_1[6], in_2[3]);
  FULL_ADDER full_adder_8 (
    .A(and_12_out), .B(full_adder_17_cout), .C(full_adder_18_cout), .S(full_adder_8_s),
    .Cout(full_adder_8_cout));
  and and_14 (and_14_out, in_1[6], in_2[4]);
  FULL_ADDER full_adder_9 (
    .A(and_4_out), .B(full_adder_8_cout), .C(full_adder_10_cout), .S(full_adder_9_s), .Cout(full_adder_9_cout));
  FULL_ADDER full_adder_10 (
    .A(and_14_out), .B(full_adder_8_s), .C(full_adder_21_cout), .S(full_adder_10_s), .Cout(full_adder_10_cout));
  and and_15 (and_15_out, in_1[5], in_2[5]);
  FULL_ADDER full_adder_11 (
    .A(and_15_out), .B(full_adder_10_s), .C(full_adder_22_cout), .S(full_adder_11_s),
    .Cout(full_adder_11_cout));
  FULL_ADDER full_adder_12 (
    .A(and_5_out), .B(full_adder_9_s), .C(full_adder_11_cout), .S(full_adder_12_s), .Cout(full_adder_12_cout));
  and and_16 (and_16_out, in_1[4], in_2[6]);
  FULL_ADDER full_adder_13 (
    .A(and_8_out), .B(full_adder_12_s), .C(full_adder_14_cout), .S(full_adder_13_s), .Cout(full_adder_13_cout));
  FULL_ADDER full_adder_14 (
    .A(and_16_out), .B(full_adder_11_s), .C(full_adder_24_cout), .S(full_adder_14_s),
    .Cout(full_adder_14_cout));
  and and_17 (and_17_out, in_1[3], in_2[7]);
  and and_18 (and_18_out, in_1[2], in_2[7]);
  FULL_ADDER full_adder_15 (
    .A(and_17_out), .B(full_adder_14_s), .C(full_adder_27_cout), .S(full_adder_26_s[10]),
    .Cout(full_adder_15_cout));
  and and_19 (and_19_out, in_1[7], in_2[1]);
  HALF_ADDER half_adder_1 (.A(and_19_out), .B(full_adder_28_cout), .S(half_adder_1_s), .Cout(half_adder_1_cout));
  and and_20 (and_20_out, in_1[6], in_2[2]);
  FULL_ADDER full_adder_16 (
    .A(and_20_out), .B(half_adder_1_s), .C(full_adder_29_cout), .S(full_adder_16_s), .Cout(full_adder_16_cout));
  FULL_ADDER full_adder_17 (
    .A(and_11_out), .B(half_adder_1_cout), .C(full_adder_16_cout), .S(full_adder_17_s),
    .Cout(full_adder_17_cout));
  and and_21 (and_21_out, in_1[5], in_2[3]);
  FULL_ADDER full_adder_18 (
    .A(and_13_out), .B(full_adder_17_s), .C(full_adder_19_cout), .S(full_adder_18_s),
    .Cout(full_adder_18_cout));
  FULL_ADDER full_adder_19 (
    .A(and_21_out), .B(full_adder_16_s), .C(full_adder_30_cout), .S(full_adder_19_s),
    .Cout(full_adder_19_cout));
  and and_22 (and_22_out, in_1[5], in_2[4]);
  and and_23 (and_23_out, in_1[4], in_2[4]);
  FULL_ADDER full_adder_20 (
    .A(and_23_out), .B(full_adder_19_s), .C(full_adder_31_cout), .S(full_adder_20_s),
    .Cout(full_adder_20_cout));
  FULL_ADDER full_adder_21 (
    .A(and_22_out), .B(full_adder_18_s), .C(full_adder_20_cout), .S(full_adder_21_s),
    .Cout(full_adder_21_cout));
  and and_24 (and_24_out, in_1[4], in_2[5]);
  and and_25 (and_25_out, in_1[3], in_2[5]);
  FULL_ADDER full_adder_22 (
    .A(and_24_out), .B(full_adder_21_s), .C(full_adder_23_cout), .S(full_adder_22_s),
    .Cout(full_adder_22_cout));
  FULL_ADDER full_adder_23 (
    .A(and_25_out), .B(full_adder_20_s), .C(full_adder_32_cout), .S(full_adder_23_s),
    .Cout(full_adder_23_cout));
  and and_26 (and_26_out, in_1[3], in_2[6]);
  and and_27 (and_27_out, in_1[2], in_2[6]);
  FULL_ADDER full_adder_24 (
    .A(and_26_out), .B(full_adder_22_s), .C(full_adder_25_cout), .S(full_adder_24_s),
    .Cout(full_adder_24_cout));
  FULL_ADDER full_adder_25 (
    .A(and_27_out), .B(full_adder_23_s), .C(full_adder_33_cout), .S(full_adder_25_s),
    .Cout(full_adder_25_cout));
  and and_28 (and_28_out, in_1[1], in_2[7]);
  FULL_ADDER full_adder_26 (
    .A(and_28_out), .B(full_adder_25_s), .C(half_adder_2_cout), .S(full_adder_26_s[8]),
    .Cout(full_adder_26_cout));
  FULL_ADDER full_adder_27 (
    .A(and_18_out), .B(full_adder_24_s), .C(full_adder_26_cout), .S(full_adder_26_s[9]),
    .Cout(full_adder_27_cout));
  and and_29 (and_29_out, in_1[7], in_2[0]);
  and and_30 (and_30_out, in_1[6], in_2[0]);
  and and_31 (and_31_out, in_1[6], in_2[1]);
  and and_32 (and_32_out, in_1[5], in_2[1]);
  FULL_ADDER full_adder_28 (
    .A(and_31_out), .B(and_29_out), .C(full_adder_34_cout), .S(full_adder_28_s), .Cout(full_adder_28_cout));
  and and_33 (and_33_out, in_1[4], in_2[2]);
  and and_34 (and_34_out, in_1[5], in_2[2]);
  FULL_ADDER full_adder_29 (
    .A(and_34_out), .B(full_adder_28_s), .C(full_adder_37_cout), .S(full_adder_29_s),
    .Cout(full_adder_29_cout));
  and and_35 (and_35_out, in_1[3], in_2[3]);
  and and_36 (and_36_out, in_1[4], in_2[3]);
  FULL_ADDER full_adder_30 (
    .A(and_36_out), .B(full_adder_29_s), .C(full_adder_39_cout), .S(full_adder_30_s),
    .Cout(full_adder_30_cout));
  and and_37 (and_37_out, in_1[3], in_2[4]);
  and and_38 (and_38_out, in_1[2], in_2[4]);
  FULL_ADDER full_adder_31 (
    .A(and_37_out), .B(full_adder_30_s), .C(full_adder_40_cout), .S(full_adder_31_s),
    .Cout(full_adder_31_cout));
  and and_39 (and_39_out, in_1[2], in_2[5]);
  and and_40 (and_40_out, in_1[1], in_2[5]);
  FULL_ADDER full_adder_32 (
    .A(and_39_out), .B(full_adder_31_s), .C(full_adder_42_cout), .S(full_adder_32_s),
    .Cout(full_adder_32_cout));
  and and_41 (and_41_out, in_1[1], in_2[6]);
  and and_42 (and_42_out, in_1[0], in_2[6]);
  FULL_ADDER full_adder_33 (
    .A(and_41_out), .B(full_adder_32_s), .C(half_adder_4_cout), .S(full_adder_33_s), .Cout(full_adder_33_cout));
  and and_43 (and_43_out, in_1[0], in_2[7]);
  HALF_ADDER half_adder_2 (.A(and_43_out), .B(full_adder_33_s), .S(out_3[7]), .Cout(half_adder_2_cout));
  and and_44 (and_44_out, in_1[5], in_2[0]);
  and and_45 (and_45_out, in_1[4], in_2[1]);
  FULL_ADDER full_adder_34 (
    .A(and_32_out), .B(and_30_out), .C(full_adder_35_cout), .S(full_adder_34_s), .Cout(full_adder_34_cout));
  FULL_ADDER full_adder_35 (
    .A(and_45_out), .B(and_44_out), .C(full_adder_43_cout), .S(full_adder_35_s), .Cout(full_adder_35_cout));
  and and_46 (and_46_out, in_1[3], in_2[2]);
  FULL_ADDER full_adder_36 (
    .A(and_46_out), .B(full_adder_35_s), .C(full_adder_45_cout), .S(full_adder_36_s),
    .Cout(full_adder_36_cout));
  FULL_ADDER full_adder_37 (
    .A(and_33_out), .B(full_adder_34_s), .C(full_adder_36_cout), .S(full_adder_37_s),
    .Cout(full_adder_37_cout));
  and and_47 (and_47_out, in_1[2], in_2[3]);
  FULL_ADDER full_adder_38 (
    .A(and_47_out), .B(full_adder_36_s), .C(full_adder_47_cout), .S(full_adder_38_s),
    .Cout(full_adder_38_cout));
  FULL_ADDER full_adder_39 (
    .A(and_35_out), .B(full_adder_37_s), .C(full_adder_38_cout), .S(full_adder_39_s),
    .Cout(full_adder_39_cout));
  and and_48 (and_48_out, in_1[1], in_2[4]);
  FULL_ADDER full_adder_40 (
    .A(and_38_out), .B(full_adder_39_s), .C(full_adder_41_cout), .S(full_adder_40_s),
    .Cout(full_adder_40_cout));
  FULL_ADDER full_adder_41 (
    .A(and_48_out), .B(full_adder_38_s), .C(half_adder_6_cout), .S(full_adder_41_s), .Cout(full_adder_41_cout));
  and and_49 (and_49_out, in_1[0], in_2[5]);
  HALF_ADDER half_adder_3 (.A(and_49_out), .B(full_adder_41_s), .S(out_3[5]), .Cout(half_adder_3_cout));
  FULL_ADDER full_adder_42 (
    .A(and_40_out), .B(full_adder_40_s), .C(half_adder_3_cout), .S(full_adder_42_s), .Cout(full_adder_42_cout));
  HALF_ADDER half_adder_4 (.A(and_42_out), .B(full_adder_42_s), .S(out_3[6]), .Cout(half_adder_4_cout));
  and and_50 (and_50_out, in_1[3], in_2[0]);
  and and_51 (and_51_out, in_1[4], in_2[0]);
  and and_52 (and_52_out, in_1[2], in_2[1]);
  and and_53 (and_53_out, in_1[3], in_2[1]);
  FULL_ADDER full_adder_43 (
    .A(and_53_out), .B(and_51_out), .C(full_adder_44_cout), .S(full_adder_43_s), .Cout(full_adder_43_cout));
  FULL_ADDER full_adder_44 (
    .A(and_52_out), .B(and_50_out), .C(full_adder_48_cout), .S(full_adder_44_s), .Cout(full_adder_44_cout));
  and and_54 (and_54_out, in_1[1], in_2[2]);
  and and_55 (and_55_out, in_1[2], in_2[2]);
  FULL_ADDER full_adder_45 (
    .A(and_55_out), .B(full_adder_43_s), .C(full_adder_46_cout), .S(full_adder_45_s),
    .Cout(full_adder_45_cout));
  FULL_ADDER full_adder_46 (
    .A(and_54_out), .B(full_adder_44_s), .C(half_adder_7_cout), .S(full_adder_46_s), .Cout(full_adder_46_cout));
  and and_56 (and_56_out, in_1[0], in_2[3]);
  and and_57 (and_57_out, in_1[1], in_2[3]);
  HALF_ADDER half_adder_5 (.A(and_56_out), .B(full_adder_46_s), .S(out_3[3]), .Cout(half_adder_5_cout));
  FULL_ADDER full_adder_47 (
    .A(and_57_out), .B(full_adder_45_s), .C(half_adder_5_cout), .S(full_adder_47_s), .Cout(full_adder_47_cout));
  and and_58 (and_58_out, in_1[0], in_2[4]);
  HALF_ADDER half_adder_6 (.A(and_58_out), .B(full_adder_47_s), .S(out_3[4]), .Cout(half_adder_6_cout));
  and and_59 (and_59_out, in_1[2], in_2[0]);
  and and_60 (and_60_out, in_1[1], in_2[0]);
  and and_61 (and_61_out, in_1[1], in_2[1]);
  and and_62 (and_62_out, in_1[0], in_2[1]);
  FULL_ADDER full_adder_48 (
    .A(and_61_out), .B(and_59_out), .C(half_adder_8_cout), .S(full_adder_48_s), .Cout(full_adder_48_cout));
  and and_63 (and_63_out, in_1[0], in_2[2]);
  HALF_ADDER half_adder_7 (.A(and_63_out), .B(full_adder_48_s), .S(out_3[2]), .Cout(half_adder_7_cout));
  and and_64 (out_3[0], in_1[0], in_2[0]);
  HALF_ADDER half_adder_8 (.A(and_62_out), .B(and_60_out), .S(out_3[1]), .Cout(half_adder_8_cout));

  // Other names for the same wires on the sheet: A0 = in_1[0]; A1 = in_1[1]; A2 = in_1[2]; A3 = in_1[3]; A4 = in_1[4];
  //   A5 = in_1[5]; A6 = in_1[6]; A7 = in_1[7]; B0 = in_2[0]; B1 = in_2[1]; B2 = in_2[2]; B3 = in_2[3]; B4 = in_2[4];
  //   B5 = in_2[5]; B6 = in_2[6]; B7 = in_2[7]
endmodule

module FULL_ADDER (
  input  A,
  input  B,
  input  C,
  output S,
  output Cout
);

  wire and_1_out, and_2_out, and_3_out, and_4_out, and_5_out, and_6_out, and_7_out, not_1_out, not_2_out,
       not_3_out, not_4_out, not_5_out, not_6_out;

  not not_1 (not_1_out, A);
  not not_2 (not_2_out, B);
  not not_3 (not_3_out, A);
  not not_4 (not_4_out, C);
  not not_5 (not_5_out, B);
  not not_6 (not_6_out, C);
  and and_1 (and_1_out, B, C);
  and and_2 (and_2_out, A, C);
  and and_3 (and_3_out, A, B);
  and and_4 (and_4_out, not_1_out, not_2_out, C);
  and and_5 (and_5_out, not_3_out, B, not_4_out);
  and and_6 (and_6_out, A, not_5_out, not_6_out);
  and and_7 (and_7_out, A, B, C);
  or or_1 (Cout, and_1_out, and_2_out, and_3_out);
  or or_2 (S, and_4_out, and_5_out, and_6_out, and_7_out);
endmodule

module HALF_ADDER (
  input  A,
  input  B,
  output S,
  output Cout
);

  wire and_2_out, and_3_out, not_1_out, not_2_out;

  not not_1 (not_1_out, A);
  not not_2 (not_2_out, B);
  and and_1 (Cout, A, B);
  and and_2 (and_2_out, not_1_out, B);
  and and_3 (and_3_out, A, not_2_out);
  or or_1 (S, and_2_out, and_3_out);
endmodule
