// Logisim project projeto-ula.circ as structural Verilog: 5 circuits, main circuit main
// Processador
module main (
  input  [7:0] in_1,
  input  [7:0] in_2,
  input  [3:0] in_3,
  input  in_4,
  input  in_5,
  output [2:0] out_6,
  output [7:0] out_7
);

  wire [7:0] aula_20_04_1_p3, divisor_1_out_4, divisor_2_out_3, gravaimpar_1_out_3, gravamaior_1_out_3,
       gravamenor_1_out_3, result, somador_1_out_4, somador_2_out_4;

  somador somador_1 (.in_1(in_1), .in_2(in_2), .in_3(1'b0), .out_4(somador_1_out_4));  // open: out_5
  somador somador_2 (.in_1(in_1), .in_2(in_2), .in_3(1'b1), .out_4(somador_2_out_4));  // open: out_5
  divisor divisor_1 (.out_4(divisor_1_out_4), .in_1(in_1), .in_2(in_2));  // open: out_3
  // aula_20_04 aula_20_04_1: pin names not known; wires that end beside it: in_1, in_2, aula_20_04_1_p3
  divisor divisor_2 (.out_3(divisor_2_out_3), .in_1(in_1), .in_2(in_2));  // open: out_4
  gravaImpar gravaimpar_1 (.in_1({8{1'b0}}), .in_2(in_1), .out_3(gravaimpar_1_out_3));
  gravaMaior gravamaior_1 (.in_1(in_1), .in_2(in_2), .out_3(gravamaior_1_out_3));
  gravaMenor gravamenor_1 (.in_1(in_1), .in_2(in_2), .out_3(gravamenor_1_out_3));
  Multiplexer #(.select(4), .width(8), .enable("false")) multiplexer_1 (
    .in0(somador_1_out_4), .in1(somador_2_out_4), .in2(divisor_1_out_4), .in3(aula_20_04_1_p3),
    .in4(divisor_2_out_3), .in5(gravaimpar_1_out_3), .in6(gravamaior_1_out_3), .in7(gravamenor_1_out_3),
    .out(result), .sel(in_3));  // open: in8, in9, in10, in11, in12, in13, in14, in15
  // cont7 cont7_1: pin names not known; wires that end beside it: in_5, out_6, out_6
  // ula_main main_1: pin names not known; wires that end beside it: in_4, result, out_7

  // Other names for the same wires on the sheet: n1[7:0] = in_1; n2[7:0] = in_2

  // Notes on the sheet:
  //   Adição
  //   Subtração
  //   Divisão
  //   Multiplicação
  //   Resto da Divisão
  //   Grava Impar
  //   Grava o Maior
  //   Grava o Menor
endmodule

module ULA (
  input  [7:0] Numero_1,
  input  [7:0] Numero_2,
  input  [3:0] \Operação ,
  output [2:0] \Posição_Na_Memória ,
  output [7:0] \Memória 
);

  wire Gravar_Resultado_out, \Muda_Posição_Na_Memória_out ;

  main main_1 (
    .in_4(Gravar_Resultado_out), .in_1(Numero_1), .in_5(\Muda_Posição_Na_Memória_out ), .in_2(Numero_2),
    .out_6(\Posição_Na_Memória ), .out_7(\Memória ), .in_3(\Operação ));
  Button \Muda_Posição_Na_Memória  (.out(\Muda_Posição_Na_Memória_out ));
  Button Gravar_Resultado (.out(Gravar_Resultado_out));

  // Notes on the sheet:
  //   0000 -  Adição
  //   0001 -  Subtração
  //   0010 -  Divisão
  //   0011 - Multiplicação
  //   0100 - Resto da Divisão
  //   0101 - Grava se Impar
  //   0110 - Grava o Maior
  //   0111 - Grava o Menor
  //   OPERAÇÕES
  //   Grava se Impar - Grava o numero 1 se ele for impar
  //   Grava o Maior - Coloca na memoria o maior entre os dois numeros indicador
  //   Grava o Menor - Coloca na memoria o menor entre os dois numeros indicador
endmodule

module gravaImpar (
  input  [7:0] in_1,
  input  [7:0] in_2,
  output [7:0] out_3
);

  wire and_1_out;

  Multiplexer #(.width(8), .enable("false")) multiplexer_1 (.in0(in_1), .in1(in_2), .out(out_3), .sel(and_1_out));
  and and_1 (and_1_out, in_2[0], 1'b1);
endmodule

module gravaMaior (
  input  [7:0] in_1,
  input  [7:0] in_2,
  output [7:0] out_3
);

  wire s;

  Multiplexer #(.width(8), .enable("false")) multiplexer_1 (.in0(in_1), .in1(in_2), .out(out_3), .sel(s));
  somador somador_1 (.in_1(in_1), .in_2(in_2), .in_3(1'b1), .out_5(s));  // open: out_4

  // Other names for the same wires on the sheet: n1[7:0] = in_1; n2[7:0] = in_2
endmodule

module gravaMenor (
  input  [7:0] in_1,
  input  [7:0] in_2,
  output [7:0] out_3
);

  wire not_1_out, s;

  not not_1 (not_1_out, s);
  Multiplexer #(.width(8), .enable("false")) multiplexer_1 (.in0(in_1), .in1(in_2), .out(out_3), .sel(not_1_out));
  somador somador_1 (.in_1(in_1), .in_2(in_2), .in_3(1'b1), .out_5(s));  // open: out_4

  // Other names for the same wires on the sheet: n1[7:0] = in_1; n2[7:0] = in_2
endmodule
