// Logisim project ula.circ as structural Verilog: 16 circuits, main circuit MAIN
// 000
module MAIN (
  input  [7:0] in_1,
  input  [7:0] in_2,
  input  [7:0] in_3,
  input  [7:0] in_4,
  input  [7:0] in_5,
  input  [7:0] in_6,
  input  [7:0] in_7,
  input  [7:0] in_8,
  output [2:0] out_9
);

  wire and_2_out, button_1_out, button_2_out, button_3_out, clock_1_out, display_1_out_3, display_1_out_4,
       display_1_out_6, display_1_out_7, display_1_out_9, display_1_out_10, display_1_out_11,
       display_2_out_3, display_2_out_4, display_2_out_6, display_2_out_7, display_2_out_9, display_2_out_10,
       display_2_out_11, display_3_out_3, display_3_out_4, display_3_out_6, display_3_out_7, display_3_out_9,
       display_3_out_10, display_3_out_11, GV, MP, not_1_out, Reset_out, vn;
  wire [2:0] OP;
  wire [3:0] display_1_out_2, display_1_out_5, display_1_out_8, display_2_out_2, display_2_out_5,
       display_2_out_8, display_3_out_2, display_3_out_5, display_3_out_8;
  wire [7:0] _000_out_4, _001_out_4, _010_out_4, _011_out_3, _100_out_3, _101_out_3, _110_out_3, _111_out_1,
       A, \Memória_out_4 , multiplexer_1_out, N, R;

  _7_Segment_Display u_7_segment_display_1 (
    .g(display_1_out_3), .f(display_1_out_9), .a(display_1_out_10), .b(display_1_out_11),
    .e(display_1_out_4), .d(display_1_out_6), .c(display_1_out_7));  // open: dp
  Hex_Digit_Display hex_digit_display_1 (.value(display_1_out_2));  // open: dp
  Hex_Digit_Display hex_digit_display_2 (.value(display_1_out_8));  // open: dp
  Hex_Digit_Display hex_digit_display_3 (.value(display_1_out_5));  // open: dp
  _7_Segment_Display u_7_segment_display_2 (
    .g(display_2_out_3), .f(display_2_out_9), .a(display_2_out_10), .b(display_2_out_11),
    .e(display_2_out_4), .d(display_2_out_6), .c(display_2_out_7));  // open: dp
  DISPLAY display_1 (
    .out_2(display_1_out_2), .out_5(display_1_out_5), .out_8(display_1_out_8), .in_1(N),
    .out_4(display_1_out_4), .out_3(display_1_out_3), .out_6(display_1_out_6), .out_7(display_1_out_7),
    .out_9(display_1_out_9), .out_10(display_1_out_10), .out_11(display_1_out_11));
  SOMADOR _000 (.in_1(A), .in_2(N), .in_3(1'b0), .out_4(_000_out_4));  // open: out_5
  SOMADOR _001 (.in_1(A), .in_2(N), .in_3(1'b1), .out_4(_001_out_4));  // open: out_5
  DIVISOR _010 (.in_1(A), .in_2(N), .out_4(_010_out_4));  // open: out_3
  MULTIPLICADOR_8_BITS _011 (.in_1(A), .in_2(N), .out_3(_011_out_3));
  gravaMaior _100 (.in_1(A), .in_2(N), .out_3(_100_out_3));
  gravaMenor _101 (.in_1(A), .in_2(N), .out_3(_101_out_3));
  DIVISOR _110 (.out_3(_110_out_3), .in_1(A), .in_2(N));  // open: out_4
  reset _111 (.out_1(_111_out_1));
  Multiplexer #(.select(3), .width(8), .enable("false")) multiplexer_1 (
    .in0(in_1), .in1(in_2), .in2(in_3), .in3(in_4), .in4(in_5), .in5(in_6), .in6(in_7), .in7(in_8),
    .out(multiplexer_1_out), .sel(out_9));
  Hex_Digit_Display hex_digit_display_4 (.value(display_2_out_2));  // open: dp
  Hex_Digit_Display hex_digit_display_5 (.value(display_2_out_5));  // open: dp
  DISPLAY display_2 (
    .out_2(display_2_out_2), .out_5(display_2_out_5), .out_8(display_2_out_8), .in_1({{5{1'b0}}, OP}),
    .out_4(display_2_out_4), .out_3(display_2_out_3), .out_6(display_2_out_6), .out_7(display_2_out_7),
    .out_9(display_2_out_9), .out_10(display_2_out_10), .out_11(display_2_out_11));
  Hex_Digit_Display hex_digit_display_6 (.value(display_2_out_8));  // open: dp
  Multiplexer #(.select(3), .width(8), .enable("false")) multiplexer_2 (
    .in0(_000_out_4), .in1(_001_out_4), .in2(_010_out_4), .in3(_011_out_3), .in4(_100_out_3),
    .in5(_101_out_3), .in6(_110_out_3), .in7(_111_out_1), .out(R), .sel(OP));
  _7_Segment_Display u_7_segment_display_3 (
    .g(display_3_out_3), .f(display_3_out_9), .a(display_3_out_10), .b(display_3_out_11),
    .e(display_3_out_4), .d(display_3_out_6), .c(display_3_out_7));  // open: dp
  Hex_Digit_Display hex_digit_display_7 (.value(display_3_out_2));  // open: dp
  Button Reset (.out(Reset_out));
  ACUMULADOR acumulador_1 (.in_1(R), .out_4(A), .in_2(button_1_out), .in_3(Reset_out));
  Button button_1 (.out(button_1_out));
  // AND_Gate and_1 has open pins: in0=button_1_out, in1=vn, out=open
  // SWITCH switch_1: pin names not known; wires that end beside it: MP, out_9
  Hex_Digit_Display hex_digit_display_8 (.value(display_3_out_8));  // open: dp
  Hex_Digit_Display hex_digit_display_9 (.value(display_3_out_5));  // open: dp
  DISPLAY display_3 (
    .out_2(display_3_out_2), .out_5(display_3_out_5), .out_8(display_3_out_8), .in_1(A),
    .out_4(display_3_out_4), .out_3(display_3_out_3), .out_6(display_3_out_6), .out_7(display_3_out_7),
    .out_9(display_3_out_9), .out_10(display_3_out_10), .out_11(display_3_out_11));
  MEMORIA \Memória  (.in_3(GV), .in_1(out_9), .in_2(multiplexer_1_out), .out_4(\Memória_out_4 ));
  separaraOperador separaraoperador_1 (.in_1(\Memória_out_4 ), .out_2(N), .out_3(OP), .out_4(vn));
  Clock clock_1 (.out(clock_1_out));
  Button button_2 (.out(button_2_out));
  not not_1 (not_1_out, vn);
  or or_1 (MP, button_2_out, button_3_out, and_2_out);
  and and_2 (and_2_out, clock_1_out, not_1_out);
  or or_2 (GV, and_2_out, button_3_out);
  Button button_3 (.out(button_3_out));
  // OR_Gate or_3 is placed but not wired

  // Other names for the same wires on the sheet: op_t[2:0] = OP

  // Notes on the sheet:
  //   Adição
  //   Subtração
  //   Divisão
  //   Multiplicação
  //   gravaMenor
  //   gravaMaior
  //   Resto Divisao
  //   Reset
  //   UNIDADE LÓGICA ARITMÉTICA
  //   Numero
  //   Operação
  //   AUTORES:
  //   DIOGO RODRIGUES
  //   VITOR HUGO
  //   Executa
  //   Operação
  //   Muda
  //   Posição
  //   Resultado
  //   OP: Operação
  //   N : Numero
  //   R : Resultado
  //   A : Acumulador
  //   Separa
  //   Operador
endmodule

module CATCH_IMPAR (
  input  [7:0] in_1,
  input  [7:0] in_2,
  output [7:0] out_3
);

  wire and_1_out;

  Multiplexer #(.width(8), .enable("false")) multiplexer_1 (.in0(in_1), .in1(in_2), .out(out_3), .sel(and_1_out));
  and and_1 (and_1_out, in_2[0], 1'b1);
endmodule

module GRAVA_MAIOR (
  input  [7:0] in_1,
  input  [7:0] in_2,
  output [7:0] out_3
);

  wire s;

  Multiplexer #(.width(8), .enable("false")) multiplexer_1 (.in0(in_1), .in1(in_2), .out(out_3), .sel(s));
  SOMADOR somador_1 (.in_1(in_1), .in_2(in_2), .in_3(1'b1), .out_5(s));  // open: out_4

  // Other names for the same wires on the sheet: n1[7:0] = in_1; n2[7:0] = in_2
endmodule

module GRAVA_MENOR (
  input  [7:0] in_1,
  input  [7:0] in_2,
  output [7:0] out_3
);

  wire not_1_out, s;

  not not_1 (not_1_out, s);
  Multiplexer #(.width(8), .enable("false")) multiplexer_1 (.in0(in_1), .in1(in_2), .out(out_3), .sel(not_1_out));
  SOMADOR somador_1 (.in_1(in_1), .in_2(in_2), .in_3(1'b1), .out_5(s));  // open: out_4

  // Other names for the same wires on the sheet: n1[7:0] = in_1; n2[7:0] = in_2
endmodule

module SOMADOR (
  input  [7:0] in_1,
  input  [7:0] in_2,
  input  in_3,
  output [7:0] out_4,
  output out_5
);

  wire and_1_out, and_2_out, and_3_out, and_4_out, and_5_out, and_6_out, and_7_out, and_8_out, and_9_out,
       and_10_out, and_11_out, and_12_out, and_13_out, and_14_out, and_15_out, and_16_out, and_17_out,
       and_18_out, and_19_out, and_20_out, and_21_out, and_22_out, and_23_out, and_24_out, and_25_out,
       and_26_out, and_27_out, and_28_out, G0_out, G1_out, G2_out, G3_out, G4_out, G5_out, G6_out, or_1_out,
       or_2_out, or_3_out, or_4_out, or_5_out, or_6_out, or_7_out, P0_out, P1_out, P2_out, P3_out, P4_out,
       P5_out, P6_out;
  wire [7:0] xor_1_out;

  assign xor_1_out = in_2 ^ {8{in_3}};  // XOR_Gate xor_1, 8 bits wide
  A_XOR_B_XOR_C a_xor_b_xor_c_1 (.S(out_4[0]), .A(xor_1_out[0]), .B(in_1[0]), .C(in_3));
  A_XOR_B_XOR_C a_xor_b_xor_c_2 (.S(out_4[1]), .A(in_1[1]), .B(xor_1_out[1]), .C(or_1_out));
  or P0 (P0_out, in_1[0], xor_1_out[0]);
  and G0 (G0_out, in_1[0], xor_1_out[0]);
  and and_1 (and_1_out, P0_out, in_3);
  or or_1 (or_1_out, G0_out, and_1_out);
  A_XOR_B_XOR_C a_xor_b_xor_c_3 (.S(out_4[2]), .A(in_1[2]), .B(xor_1_out[2]), .C(or_2_out));
  and G1 (G1_out, in_1[1], xor_1_out[1]);
  or or_2 (or_2_out, G1_out, and_2_out, and_3_out);
  or P1 (P1_out, in_1[1], xor_1_out[1]);
  and and_2 (and_2_out, P1_out, G0_out);
  and and_3 (and_3_out, P1_out, P0_out, in_3);
  A_XOR_B_XOR_C a_xor_b_xor_c_4 (.S(out_4[3]), .A(in_1[3]), .B(xor_1_out[3]), .C(or_3_out));
  or P2 (P2_out, in_1[2], xor_1_out[2]);
  and G2 (G2_out, in_1[2], xor_1_out[2]);
  and and_4 (and_4_out, P2_out, G1_out);
  or or_3 (or_3_out, G2_out, and_4_out, and_5_out, and_6_out);
  and and_5 (and_5_out, G0_out, P1_out, P2_out);
  and and_6 (and_6_out, in_3, P0_out, P1_out, P2_out);
  A_XOR_B_XOR_C a_xor_b_xor_c_5 (.S(out_4[4]), .A(in_1[4]), .B(xor_1_out[4]), .C(or_4_out));
  and G3 (G3_out, in_1[3], xor_1_out[3]);
  or or_4 (or_4_out, G3_out, and_8_out, and_7_out, and_9_out, and_10_out);
  or P3 (P3_out, in_1[3], xor_1_out[3]);
  and and_7 (and_7_out, G1_out, P2_out, P3_out);
  and and_8 (and_8_out, P3_out, G2_out);
  and and_9 (and_9_out, G0_out, P1_out, P2_out, P3_out);
  and and_10 (and_10_out, in_3, P0_out, P1_out, P2_out, P3_out);
  and G4 (G4_out, in_1[4], xor_1_out[4]);
  A_XOR_B_XOR_C a_xor_b_xor_c_6 (.S(out_4[5]), .A(in_1[5]), .B(xor_1_out[5]), .C(or_5_out));
  or P4 (P4_out, in_1[4], xor_1_out[4]);
  and and_11 (and_11_out, G2_out, P3_out, P4_out);
  and and_12 (and_12_out, P4_out, G3_out);
  or or_5 (or_5_out, G4_out, and_12_out, and_11_out, and_13_out, and_14_out, and_15_out);
  and and_13 (and_13_out, G1_out, P2_out, P3_out, P4_out);
  and and_14 (and_14_out, G0_out, P1_out, P2_out, P3_out, P4_out);
  and and_15 (and_15_out, in_3, P0_out, P1_out, P2_out, P3_out, P4_out);
  A_XOR_B_XOR_C a_xor_b_xor_c_7 (.S(out_4[6]), .A(in_1[6]), .B(xor_1_out[6]), .C(or_6_out));
  and G5 (G5_out, in_1[5], xor_1_out[5]);
  or P5 (P5_out, in_1[5], xor_1_out[5]);
  and and_16 (and_16_out, P5_out, G4_out);
  or or_6 (or_6_out, G5_out, and_16_out, and_17_out, and_18_out, and_19_out, and_20_out, and_21_out);
  and and_17 (and_17_out, G3_out, P4_out, P5_out);
  and and_18 (and_18_out, G2_out, P3_out, P4_out, P5_out);
  and and_19 (and_19_out, G1_out, P2_out, P3_out, P4_out, P5_out);
  and and_20 (and_20_out, G0_out, P1_out, P2_out, P3_out, P4_out, P5_out);
  and and_21 (and_21_out, in_3, P0_out, P1_out, P2_out, P3_out, P4_out, P5_out);
  A_XOR_B_XOR_C a_xor_b_xor_c_8 (.S(out_4[7]), .A(in_1[7]), .B(xor_1_out[7]), .C(or_7_out));
  and G6 (G6_out, in_1[6], xor_1_out[6]);
  or P6 (P6_out, in_1[6], xor_1_out[6]);
  and and_22 (and_22_out, P6_out, G5_out);
  or or_7 (or_7_out, G6_out, and_22_out, and_24_out, and_23_out, and_25_out, and_26_out, and_27_out, and_28_out);
  and and_23 (and_23_out, G3_out, P4_out, P5_out, P6_out);
  and and_24 (and_24_out, G4_out, P5_out, P6_out);
  and and_25 (and_25_out, G2_out, P3_out, P4_out, P5_out, P6_out);
  and and_26 (and_26_out, G1_out, P2_out, P3_out, P4_out, P5_out, P6_out);
  and and_27 (and_27_out, G0_out, P1_out, P2_out, P3_out, P4_out, P5_out, P6_out);
  and and_28 (and_28_out, in_3, P0_out, P1_out, P2_out, P3_out, P4_out, P5_out, P6_out);

  assign out_5 = out_4[7];
endmodule

module A_XOR_B_XOR_C (
  input  A,
  input  B,
  input  C,
  output S
);

  wire xor_1_out;

  xor xor_1 (xor_1_out, C, B);
  xor xor_2 (S, xor_1_out, A);
endmodule

module DIVISOR (
  input  [7:0] in_1,
  input  [7:0] in_2,
  output [7:0] out_3,
  output [7:0] out_4
);

  wire somador_1_out_5, somador_2_out_5, somador_3_out_5, somador_4_out_5, somador_5_out_5, somador_6_out_5,
       somador_7_out_5, somador_8_out_5;
  wire [7:0] multiplexer_1_out, multiplexer_2_out, multiplexer_3_out, multiplexer_4_out, multiplexer_5_out,
       multiplexer_7_out, somador_1_out_4, somador_2_out_4, somador_3_out_4, somador_4_out_4,
       somador_5_out_4, somador_6_out_4, somador_7_out_4, somador_8_out_4;
  wire [7:1] multiplexer_6_out_2;
  wire [7:7] multiplexer_6_out;

  SOMADOR somador_1 (
    .in_1({{7{1'b0}}, in_1[7]}), .in_2(in_2), .in_3(1'b1), .out_4(somador_1_out_4), .out_5(somador_1_out_5));
  Multiplexer #(.width(8), .enable("false")) multiplexer_1 (
    .in0(somador_1_out_4), .in1({{7{1'b0}}, in_1[7]}), .out(multiplexer_1_out), .sel(somador_1_out_5));
  SOMADOR somador_2 (
    .in_1({multiplexer_1_out[6:0], in_1[6]}), .in_2(in_2), .in_3(1'b1), .out_4(somador_2_out_4),
    .out_5(somador_2_out_5));
  Multiplexer #(.width(8), .enable("false")) multiplexer_2 (
    .in0(somador_2_out_4), .in1({multiplexer_1_out[6:0], in_1[6]}), .out(multiplexer_2_out),
    .sel(somador_2_out_5));
  not not_1 (out_4[7], somador_1_out_5);
  not not_2 (out_4[5], somador_3_out_5);
  not not_3 (out_4[6], somador_2_out_5);
  not not_4 (out_4[1], somador_7_out_5);
  not not_5 (out_4[3], somador_5_out_5);
  not not_6 (out_4[2], somador_6_out_5);
  not not_7 (out_4[4], somador_4_out_5);
  not not_8 (out_4[0], somador_8_out_5);
  SOMADOR somador_3 (
    .in_1({multiplexer_2_out[6:0], in_1[5]}), .in_2(in_2), .in_3(1'b1), .out_4(somador_3_out_4),
    .out_5(somador_3_out_5));
  Multiplexer #(.width(8), .enable("false")) multiplexer_3 (
    .in0(somador_3_out_4), .in1({multiplexer_2_out[6:0], in_1[5]}), .out(multiplexer_3_out),
    .sel(somador_3_out_5));
  SOMADOR somador_4 (
    .in_1({multiplexer_3_out[6:0], in_1[4]}), .in_2(in_2), .in_3(1'b1), .out_4(somador_4_out_4),
    .out_5(somador_4_out_5));
  Multiplexer #(.width(8), .enable("false")) multiplexer_4 (
    .in0(somador_4_out_4), .in1({multiplexer_3_out[6:0], in_1[4]}), .out(multiplexer_4_out),
    .sel(somador_4_out_5));
  SOMADOR somador_5 (
    .in_1({multiplexer_4_out[6:0], in_1[3]}), .in_2(in_2), .in_3(1'b1), .out_4(somador_5_out_4),
    .out_5(somador_5_out_5));
  Multiplexer #(.width(8), .enable("false")) multiplexer_5 (
    .in0(somador_5_out_4), .in1({multiplexer_4_out[6:0], in_1[3]}), .out(multiplexer_5_out),
    .sel(somador_5_out_5));
  SOMADOR somador_6 (
    .in_1({multiplexer_5_out[6:0], in_1[2]}), .in_2(in_2), .in_3(1'b1), .out_4(somador_6_out_4),
    .out_5(somador_6_out_5));
  Multiplexer #(.width(8), .enable("false")) multiplexer_6 (
    .in0(somador_6_out_4), .in1({multiplexer_5_out[6:0], in_1[2]}),
    .out({multiplexer_6_out[7], multiplexer_6_out_2}), .sel(somador_6_out_5));
  SOMADOR somador_7 (
    .in_1({multiplexer_6_out_2, in_1[1]}), .in_2(in_2), .in_3(1'b1), .out_4(somador_7_out_4),
    .out_5(somador_7_out_5));
  Multiplexer #(.width(8), .enable("false")) multiplexer_7 (
    .in0(somador_7_out_4), .in1({multiplexer_6_out_2, in_1[1]}), .out(multiplexer_7_out),
    .sel(somador_7_out_5));
  SOMADOR somador_8 (
    .in_1({multiplexer_7_out[6:0], in_1[0]}), .in_2(in_2), .in_3(1'b1), .out_4(somador_8_out_4),
    .out_5(somador_8_out_5));
  Multiplexer #(.width(8), .enable("false")) multiplexer_8 (
    .in0(somador_8_out_4), .in1({multiplexer_7_out[6:0], in_1[0]}), .out(out_3), .sel(somador_8_out_5));

  // Other names for the same wires on the sheet: Dividendo[7:0] = in_1; Divisor[7:0] = in_2; Resto[7:0] = out_3;
  //   Resultado[7:0] = out_4
endmodule

module FULL_ADDER (
  input  A,
  input  B,
  input  C,
  output S,
  output Cout
);

  wire and_1_out, and_2_out, and_3_out, and_4_out, and_5_out, and_6_out, and_7_out, not_1_out, not_2_out,
       not_3_out, not_4_out, not_5_out, not_6_out;

  not not_1 (not_1_out, A);
  not not_2 (not_2_out, B);
  not not_3 (not_3_out, A);
  not not_4 (not_4_out, C);
  not not_5 (not_5_out, B);
  not not_6 (not_6_out, C);
  and and_1 (and_1_out, B, C);
  and and_2 (and_2_out, A, C);
  and and_3 (and_3_out, A, B);
  and and_4 (and_4_out, not_1_out, not_2_out, C);
  and and_5 (and_5_out, not_3_out, B, not_4_out);
  and and_6 (and_6_out, A, not_5_out, not_6_out);
  and and_7 (and_7_out, A, B, C);
  or or_1 (Cout, and_1_out, and_2_out, and_3_out);
  or or_2 (S, and_4_out, and_5_out, and_6_out, and_7_out);
endmodule

module HALF_ADDER (
  input  A,
  input  B,
  output S,
  output Cout
);

  wire and_2_out, and_3_out, not_1_out, not_2_out;

  not not_1 (not_1_out, A);
  not not_2 (not_2_out, B);
  and and_1 (Cout, A, B);
  and and_2 (and_2_out, not_1_out, B);
  and and_3 (and_3_out, A, not_2_out);
  or or_1 (S, and_2_out, and_3_out);
endmodule

module MULTIPLICADOR_8_BITS (
  input  [7:0] in_1,
  input  [7:0] in_2,
  output [7:0] out_3
);

  wire and_1_out, and_2_out, and_3_out, and_4_out, and_5_out, and_6_out, and_7_out, and_8_out, and_9_out,
       and_10_out, and_11_out, and_12_out, and_13_out, and_14_out, and_15_out, and_16_out, and_17_out,
       and_18_out, and_19_out, and_20_out, and_21_out, and_22_out, and_23_out, and_24_out, and_25_out,
       and_26_out, and_27_out, and_28_out, and_29_out, and_30_out, and_31_out, and_32_out, and_33_out,
       and_34_out, and_35_out, and_36_out, and_37_out, and_38_out, and_39_out, and_40_out, and_41_out,
       and_42_out, and_43_out, and_44_out, and_45_out, and_46_out, and_47_out, and_48_out, and_49_out,
       and_50_out, and_51_out, and_52_out, and_53_out, and_54_out, and_55_out, and_56_out, and_57_out,
       and_58_out, and_59_out, and_60_out, and_61_out, and_62_out, and_63_out, full_adder_2_cout,
       full_adder_2_s, full_adder_3_cout, full_adder_4_cout, full_adder_5_cout, full_adder_5_s,
       full_adder_6_cout, full_adder_6_s, full_adder_7_cout, full_adder_7_s, full_adder_8_cout,
       full_adder_8_s, full_adder_9_cout, full_adder_9_s, full_adder_10_cout, full_adder_11_cout,
       full_adder_11_s, full_adder_12_cout, full_adder_12_s, full_adder_13_cout, full_adder_13_s,
       full_adder_14_cout, full_adder_14_s, full_adder_15_cout, full_adder_15_s, full_adder_16_cout,
       full_adder_16_s, full_adder_17_cout, full_adder_17_s, full_adder_18_cout, full_adder_18_s,
       full_adder_19_cout, full_adder_19_s, full_adder_20_cout, full_adder_21_cout, full_adder_22_cout,
       full_adder_22_s, full_adder_23_cout, full_adder_23_s, full_adder_24_cout, full_adder_24_s,
       full_adder_25_cout, full_adder_25_s, full_adder_26_cout, full_adder_26_s, full_adder_27_cout,
       full_adder_28_cout, full_adder_28_s, full_adder_29_cout, full_adder_29_s, full_adder_30_cout,
       full_adder_30_s, full_adder_31_cout, full_adder_31_s, full_adder_32_cout, full_adder_32_s,
       full_adder_33_cout, full_adder_33_s, full_adder_34_cout, full_adder_34_s, full_adder_35_cout,
       full_adder_35_s, full_adder_36_cout, full_adder_36_s, full_adder_37_cout, full_adder_37_s,
       full_adder_38_cout, full_adder_38_s, full_adder_39_cout, full_adder_39_s, full_adder_40_cout,
       full_adder_40_s, full_adder_41_cout, full_adder_41_s, full_adder_42_cout, full_adder_42_s,
       full_adder_43_cout, full_adder_43_s, full_adder_44_cout, full_adder_44_s, full_adder_45_cout,
       full_adder_45_s, full_adder_46_cout, full_adder_46_s, full_adder_47_cout, full_adder_47_s,
       full_adder_48_cout, full_adder_48_s, half_adder_1_cout, half_adder_1_s, half_adder_2_cout,
       half_adder_3_cout, half_adder_4_cout, half_adder_5_cout, half_adder_6_cout, half_adder_7_cout,
       half_adder_8_cout;
  wire [15:8] full_adder_27_s;

  and and_1 (and_1_out, in_1[7], in_2[7]);
  FULL_ADDER full_adder_1 (
    .A(and_1_out), .B(full_adder_2_cout), .C(full_adder_3_cout), .S(full_adder_27_s[14]),
    .Cout(full_adder_27_s[15]));
  and and_2 (and_2_out, in_1[7], in_2[5]);
  and and_3 (and_3_out, in_1[6], in_2[6]);
  and and_4 (and_4_out, in_1[7], in_2[6]);
  FULL_ADDER full_adder_2 (
    .A(and_4_out), .B(full_adder_7_cout), .C(full_adder_9_cout), .S(full_adder_2_s), .Cout(full_adder_2_cout));
  and and_5 (and_5_out, in_1[6], in_2[7]);
  and and_6 (and_6_out, in_1[5], in_2[7]);
  FULL_ADDER full_adder_3 (
    .A(and_5_out), .B(full_adder_2_s), .C(full_adder_4_cout), .S(full_adder_27_s[13]),
    .Cout(full_adder_3_cout));
  FULL_ADDER full_adder_4 (
    .A(and_6_out), .B(full_adder_9_s), .C(full_adder_10_cout), .S(full_adder_27_s[12]),
    .Cout(full_adder_4_cout));
  and and_7 (and_7_out, in_1[7], in_2[3]);
  and and_8 (and_8_out, in_1[7], in_2[4]);
  FULL_ADDER full_adder_5 (
    .A(and_8_out), .B(full_adder_13_cout), .C(full_adder_15_cout), .S(full_adder_5_s),
    .Cout(full_adder_5_cout));
  and and_9 (and_9_out, in_1[6], in_2[5]);
  FULL_ADDER full_adder_6 (
    .A(and_9_out), .B(full_adder_5_s), .C(full_adder_16_cout), .S(full_adder_6_s), .Cout(full_adder_6_cout));
  FULL_ADDER full_adder_7 (
    .A(and_2_out), .B(full_adder_5_cout), .C(full_adder_6_cout), .S(full_adder_7_s), .Cout(full_adder_7_cout));
  and and_10 (and_10_out, in_1[5], in_2[6]);
  FULL_ADDER full_adder_8 (
    .A(and_10_out), .B(full_adder_6_s), .C(full_adder_19_cout), .S(full_adder_8_s), .Cout(full_adder_8_cout));
  FULL_ADDER full_adder_9 (
    .A(and_3_out), .B(full_adder_7_s), .C(full_adder_8_cout), .S(full_adder_9_s), .Cout(full_adder_9_cout));
  and and_11 (and_11_out, in_1[3], in_2[7]);
  and and_12 (and_12_out, in_1[4], in_2[7]);
  FULL_ADDER full_adder_10 (
    .A(and_12_out), .B(full_adder_8_s), .C(full_adder_20_cout), .S(full_adder_27_s[11]),
    .Cout(full_adder_10_cout));
  and and_13 (and_13_out, in_1[7], in_2[2]);
  FULL_ADDER full_adder_11 (
    .A(and_13_out), .B(half_adder_1_cout), .C(full_adder_22_cout), .S(full_adder_11_s),
    .Cout(full_adder_11_cout));
  and and_14 (and_14_out, in_1[6], in_2[3]);
  FULL_ADDER full_adder_12 (
    .A(and_14_out), .B(full_adder_11_s), .C(full_adder_23_cout), .S(full_adder_12_s),
    .Cout(full_adder_12_cout));
  FULL_ADDER full_adder_13 (
    .A(and_7_out), .B(full_adder_11_cout), .C(full_adder_12_cout), .S(full_adder_13_s),
    .Cout(full_adder_13_cout));
  and and_15 (and_15_out, in_1[5], in_2[4]);
  and and_16 (and_16_out, in_1[6], in_2[4]);
  FULL_ADDER full_adder_14 (
    .A(and_15_out), .B(full_adder_12_s), .C(full_adder_24_cout), .S(full_adder_14_s),
    .Cout(full_adder_14_cout));
  FULL_ADDER full_adder_15 (
    .A(and_16_out), .B(full_adder_13_s), .C(full_adder_14_cout), .S(full_adder_15_s),
    .Cout(full_adder_15_cout));
  and and_17 (and_17_out, in_1[5], in_2[5]);
  and and_18 (and_18_out, in_1[4], in_2[5]);
  FULL_ADDER full_adder_16 (
    .A(and_17_out), .B(full_adder_15_s), .C(full_adder_17_cout), .S(full_adder_16_s),
    .Cout(full_adder_16_cout));
  FULL_ADDER full_adder_17 (
    .A(and_18_out), .B(full_adder_14_s), .C(full_adder_25_cout), .S(full_adder_17_s),
    .Cout(full_adder_17_cout));
  and and_19 (and_19_out, in_1[4], in_2[6]);
  and and_20 (and_20_out, in_1[3], in_2[6]);
  FULL_ADDER full_adder_18 (
    .A(and_20_out), .B(full_adder_17_s), .C(full_adder_26_cout), .S(full_adder_18_s),
    .Cout(full_adder_18_cout));
  FULL_ADDER full_adder_19 (
    .A(and_19_out), .B(full_adder_16_s), .C(full_adder_18_cout), .S(full_adder_19_s),
    .Cout(full_adder_19_cout));
  and and_21 (and_21_out, in_1[2], in_2[7]);
  FULL_ADDER full_adder_20 (
    .A(and_11_out), .B(full_adder_19_s), .C(full_adder_21_cout), .S(full_adder_27_s[10]),
    .Cout(full_adder_20_cout));
  FULL_ADDER full_adder_21 (
    .A(and_21_out), .B(full_adder_18_s), .C(full_adder_27_cout), .S(full_adder_27_s[9]),
    .Cout(full_adder_21_cout));
  and and_22 (and_22_out, in_1[7], in_2[0]);
  and and_23 (and_23_out, in_1[7], in_2[1]);
  and and_24 (and_24_out, in_1[6], in_2[1]);
  HALF_ADDER half_adder_1 (.A(and_23_out), .B(full_adder_29_cout), .S(half_adder_1_s), .Cout(half_adder_1_cout));
  and and_25 (and_25_out, in_1[5], in_2[2]);
  and and_26 (and_26_out, in_1[6], in_2[2]);
  FULL_ADDER full_adder_22 (
    .A(and_26_out), .B(half_adder_1_s), .C(full_adder_30_cout), .S(full_adder_22_s), .Cout(full_adder_22_cout));
  and and_27 (and_27_out, in_1[5], in_2[3]);
  and and_28 (and_28_out, in_1[4], in_2[3]);
  FULL_ADDER full_adder_23 (
    .A(and_27_out), .B(full_adder_22_s), .C(full_adder_32_cout), .S(full_adder_23_s),
    .Cout(full_adder_23_cout));
  and and_29 (and_29_out, in_1[4], in_2[4]);
  and and_30 (and_30_out, in_1[3], in_2[4]);
  FULL_ADDER full_adder_24 (
    .A(and_29_out), .B(full_adder_23_s), .C(full_adder_35_cout), .S(full_adder_24_s),
    .Cout(full_adder_24_cout));
  and and_31 (and_31_out, in_1[3], in_2[5]);
  and and_32 (and_32_out, in_1[2], in_2[5]);
  FULL_ADDER full_adder_25 (
    .A(and_31_out), .B(full_adder_24_s), .C(full_adder_36_cout), .S(full_adder_25_s),
    .Cout(full_adder_25_cout));
  and and_33 (and_33_out, in_1[1], in_2[6]);
  and and_34 (and_34_out, in_1[2], in_2[6]);
  FULL_ADDER full_adder_26 (
    .A(and_34_out), .B(full_adder_25_s), .C(full_adder_38_cout), .S(full_adder_26_s),
    .Cout(full_adder_26_cout));
  and and_35 (and_35_out, in_1[0], in_2[7]);
  and and_36 (and_36_out, in_1[1], in_2[7]);
  FULL_ADDER full_adder_27 (
    .A(and_36_out), .B(full_adder_26_s), .C(half_adder_3_cout), .S(full_adder_27_s[8]),
    .Cout(full_adder_27_cout));
  and and_37 (and_37_out, in_1[6], in_2[0]);
  and and_38 (and_38_out, in_1[5], in_2[1]);
  FULL_ADDER full_adder_28 (
    .A(and_38_out), .B(and_37_out), .C(full_adder_39_cout), .S(full_adder_28_s), .Cout(full_adder_28_cout));
  FULL_ADDER full_adder_29 (
    .A(and_24_out), .B(and_22_out), .C(full_adder_28_cout), .S(full_adder_29_s), .Cout(full_adder_29_cout));
  and and_39 (and_39_out, in_1[4], in_2[2]);
  FULL_ADDER full_adder_30 (
    .A(and_25_out), .B(full_adder_29_s), .C(full_adder_31_cout), .S(full_adder_30_s),
    .Cout(full_adder_30_cout));
  FULL_ADDER full_adder_31 (
    .A(and_39_out), .B(full_adder_28_s), .C(full_adder_42_cout), .S(full_adder_31_s),
    .Cout(full_adder_31_cout));
  and and_40 (and_40_out, in_1[3], in_2[3]);
  FULL_ADDER full_adder_32 (
    .A(and_28_out), .B(full_adder_30_s), .C(full_adder_33_cout), .S(full_adder_32_s),
    .Cout(full_adder_32_cout));
  FULL_ADDER full_adder_33 (
    .A(and_40_out), .B(full_adder_31_s), .C(full_adder_44_cout), .S(full_adder_33_s),
    .Cout(full_adder_33_cout));
  and and_41 (and_41_out, in_1[2], in_2[4]);
  FULL_ADDER full_adder_34 (
    .A(and_41_out), .B(full_adder_33_s), .C(full_adder_45_cout), .S(full_adder_34_s),
    .Cout(full_adder_34_cout));
  FULL_ADDER full_adder_35 (
    .A(and_30_out), .B(full_adder_32_s), .C(full_adder_34_cout), .S(full_adder_35_s),
    .Cout(full_adder_35_cout));
  and and_42 (and_42_out, in_1[1], in_2[5]);
  FULL_ADDER full_adder_36 (
    .A(and_32_out), .B(full_adder_35_s), .C(full_adder_37_cout), .S(full_adder_36_s),
    .Cout(full_adder_36_cout));
  FULL_ADDER full_adder_37 (
    .A(and_42_out), .B(full_adder_34_s), .C(half_adder_4_cout), .S(full_adder_37_s), .Cout(full_adder_37_cout));
  and and_43 (and_43_out, in_1[0], in_2[6]);
  HALF_ADDER half_adder_2 (.A(and_43_out), .B(full_adder_37_s), .S(out_3[6]), .Cout(half_adder_2_cout));
  FULL_ADDER full_adder_38 (
    .A(and_33_out), .B(full_adder_36_s), .C(half_adder_2_cout), .S(full_adder_38_s), .Cout(full_adder_38_cout));
  HALF_ADDER half_adder_3 (.A(and_35_out), .B(full_adder_38_s), .S(out_3[7]), .Cout(half_adder_3_cout));
  and and_44 (and_44_out, in_1[5], in_2[0]);
  and and_45 (and_45_out, in_1[4], in_2[0]);
  and and_46 (and_46_out, in_1[3], in_2[1]);
  and and_47 (and_47_out, in_1[4], in_2[1]);
  FULL_ADDER full_adder_39 (
    .A(and_47_out), .B(and_44_out), .C(full_adder_40_cout), .S(full_adder_39_s), .Cout(full_adder_39_cout));
  FULL_ADDER full_adder_40 (
    .A(and_46_out), .B(and_45_out), .C(full_adder_46_cout), .S(full_adder_40_s), .Cout(full_adder_40_cout));
  and and_48 (and_48_out, in_1[2], in_2[2]);
  and and_49 (and_49_out, in_1[3], in_2[2]);
  FULL_ADDER full_adder_41 (
    .A(and_48_out), .B(full_adder_40_s), .C(full_adder_47_cout), .S(full_adder_41_s),
    .Cout(full_adder_41_cout));
  FULL_ADDER full_adder_42 (
    .A(and_49_out), .B(full_adder_39_s), .C(full_adder_41_cout), .S(full_adder_42_s),
    .Cout(full_adder_42_cout));
  and and_50 (and_50_out, in_1[1], in_2[3]);
  and and_51 (and_51_out, in_1[2], in_2[3]);
  FULL_ADDER full_adder_43 (
    .A(and_50_out), .B(full_adder_41_s), .C(half_adder_5_cout), .S(full_adder_43_s), .Cout(full_adder_43_cout));
  FULL_ADDER full_adder_44 (
    .A(and_51_out), .B(full_adder_42_s), .C(full_adder_43_cout), .S(full_adder_44_s),
    .Cout(full_adder_44_cout));
  and and_52 (and_52_out, in_1[1], in_2[4]);
  and and_53 (and_53_out, in_1[0], in_2[4]);
  FULL_ADDER full_adder_45 (
    .A(and_52_out), .B(full_adder_44_s), .C(half_adder_6_cout), .S(full_adder_45_s), .Cout(full_adder_45_cout));
  and and_54 (and_54_out, in_1[0], in_2[5]);
  HALF_ADDER half_adder_4 (.A(and_54_out), .B(full_adder_45_s), .S(out_3[5]), .Cout(half_adder_4_cout));
  and and_55 (and_55_out, in_1[2], in_2[0]);
  and and_56 (and_56_out, in_1[3], in_2[0]);
  and and_57 (and_57_out, in_1[2], in_2[1]);
  and and_58 (and_58_out, in_1[1], in_2[1]);
  FULL_ADDER full_adder_46 (
    .A(and_57_out), .B(and_56_out), .C(full_adder_48_cout), .S(full_adder_46_s), .Cout(full_adder_46_cout));
  and and_59 (and_59_out, in_1[1], in_2[2]);
  and and_60 (and_60_out, in_1[0], in_2[2]);
  FULL_ADDER full_adder_47 (
    .A(and_59_out), .B(full_adder_46_s), .C(half_adder_8_cout), .S(full_adder_47_s), .Cout(full_adder_47_cout));
  and and_61 (and_61_out, in_1[0], in_2[3]);
  HALF_ADDER half_adder_5 (.A(and_61_out), .B(full_adder_47_s), .S(out_3[3]), .Cout(half_adder_5_cout));
  HALF_ADDER half_adder_6 (.A(and_53_out), .B(full_adder_43_s), .S(out_3[4]), .Cout(half_adder_6_cout));
  and and_62 (and_62_out, in_1[1], in_2[0]);
  and and_63 (and_63_out, in_1[0], in_2[1]);
  HALF_ADDER half_adder_7 (.A(and_63_out), .B(and_62_out), .S(out_3[1]), .Cout(half_adder_7_cout));
  FULL_ADDER full_adder_48 (
    .A(and_58_out), .B(and_55_out), .C(half_adder_7_cout), .S(full_adder_48_s), .Cout(full_adder_48_cout));
  HALF_ADDER half_adder_8 (.A(and_60_out), .B(full_adder_48_s), .S(out_3[2]), .Cout(half_adder_8_cout));
  and and_64 (out_3[0], in_1[0], in_2[0]);

  // Other names for the same wires on the sheet: A0 = in_1[0]; A1 = in_1[1]; A2 = in_1[2]; A3 = in_1[3]; A4 = in_1[4];
  //   A5 = in_1[5]; A6 = in_1[6]; A7 = in_1[7]; B0 = in_2[0]; B1 = in_2[1]; B2 = in_2[2]; B3 = in_2[3]; B4 = in_2[4];
  //   B5 = in_2[5]; B6 = in_2[6]; B7 = in_2[7]
endmodule

module ACUMULADOR (
  input  [7:0] in_1,
  input  in_2,
  input  in_3,
  output [7:0] out_4
);

  D_Flip_Flop d_ff_1 (.clk(in_2), .D(in_1[7]), .Q(out_4[7]), .reset(in_3));  // open: Qn, preset, en
  D_Flip_Flop d_ff_2 (.clk(in_2), .D(in_1[6]), .Q(out_4[6]), .reset(in_3));  // open: Qn, preset, en
  D_Flip_Flop d_ff_3 (.clk(in_2), .D(in_1[5]), .Q(out_4[5]), .reset(in_3));  // open: Qn, preset, en
  D_Flip_Flop d_ff_4 (.clk(in_2), .D(in_1[4]), .Q(out_4[4]), .reset(in_3));  // open: Qn, preset, en
  D_Flip_Flop d_ff_5 (.clk(in_2), .D(in_1[3]), .Q(out_4[3]), .reset(in_3));  // open: Qn, preset, en
  D_Flip_Flop d_ff_6 (.clk(in_2), .D(in_1[2]), .Q(out_4[2]), .reset(in_3));  // open: Qn, preset, en
  D_Flip_Flop d_ff_7 (.clk(in_2), .D(in_1[1]), .Q(out_4[1]), .reset(in_3));  // open: Qn, preset, en
  D_Flip_Flop d_ff_8 (.clk(in_2), .D(in_1[0]), .Q(out_4[0]), .reset(in_3));  // open: Qn, preset, en
endmodule

module separaraOperador (
  input  [7:0] in_1,
  output [7:0] out_2,
  output [2:0] out_3,
  output out_4
);

  wire and_1_out;

  not not_1 (out_4, and_1_out);
  and and_1 (and_1_out, ~in_1[0], ~in_1[1], ~in_1[2], ~in_1[3], ~in_1[4], ~in_1[5], ~in_1[6], ~in_1[7]);  // AND_Gate

  assign out_2 = {3'b000, in_1[4:0]};
  assign out_3 = in_1[7:5];
endmodule

module DISPLAY (
  input  [7:0] in_1,
  output [3:0] out_2,
  output out_3,
  output out_4,
  output [3:0] out_5,
  output out_6,
  output out_7,
  output [3:0] out_8,
  output out_9,
  output out_10,
  output out_11
);

  wire [7:0] divider_1_rem, multiplexer_1_out, multiplier_1_out;
  wire [7:4] divider_1_out, divider_2_out, divider_2_rem;

  and and_1 (out_3, in_1[7], 1'b1);
  Multiplier multiplier_1 (.a(in_1), .b({8{1'b1}}), .out(multiplier_1_out));  // open: cin, cout
  not not_1 (out_4, out_3);
  not not_2 (out_7, out_3);
  not not_3 (out_6, out_3);
  not not_4 (out_11, out_3);
  not not_5 (out_10, out_3);
  not not_6 (out_9, out_3);
  Multiplexer #(.width(8), .enable("false")) multiplexer_1 (
    .in0(in_1), .in1(multiplier_1_out), .out(multiplexer_1_out), .sel(out_3));
  Divider divider_1 (
    .a(multiplexer_1_out), .b(8'h64), .out({divider_1_out, out_2}), .rem(divider_1_rem));  // open: upper
  Divider divider_2 (
    .a(divider_1_rem), .b(8'ha), .out({divider_2_out, out_5}), .rem({divider_2_rem, out_8}));  // open: upper
endmodule

module gravaMaior (
  input  [7:0] in_1,
  input  [7:0] in_2,
  output [7:0] out_3
);

  wire somador_1_out_5;

  SOMADOR somador_1 (.in_1(in_1), .in_2(in_2), .in_3(1'b1), .out_5(somador_1_out_5));  // open: out_4
  Multiplexer #(.width(8), .enable("false")) multiplexer_1 (.in0(in_2), .in1(in_1), .out(out_3), .sel(somador_1_out_5));
endmodule

module gravaMenor (
  input  [7:0] in_1,
  input  [7:0] in_2,
  output [7:0] out_3
);

  wire not_1_out, somador_1_out_5;

  not not_1 (not_1_out, somador_1_out_5);
  SOMADOR somador_1 (.in_1(in_1), .in_2(in_2), .in_3(1'b1), .out_5(somador_1_out_5));  // open: out_4
  Multiplexer #(.width(8), .enable("false")) multiplexer_1 (.in0(in_2), .in1(in_1), .out(out_3), .sel(not_1_out));
endmodule

module reset (
  output [7:0] out_1
);


  assign out_1 = {8{1'b0}};
endmodule
